// Logisim project BIT_MANIPULATION.circ as structural Verilog: 1 circuit, main circuit BIT_MANIPULATION
module BIT_MANIPULATION (
  input  [7:0] val_in,
  input  start,
  output [7:0] val_1,
  output [7:0] val2,
  output stop
);

  wire not_1_out;

  not not_1 (not_1_out, start);
  not not_2 (stop, not_1_out);

  assign val2 = {val_in[6:0], 1'b0};
  assign val_1 = {1'b0, val_in[7:1]};
endmodule
