// Logisim project BUT_TO_BINv2.circ as structural Verilog: 1 circuit, main circuit BUT_TO_BIN
module BUT_TO_BIN (
  input  _1,
  input  _2,
  input  _3,
  input  _4,
  input  _5,
  input  _6,
  input  _7,
  input  _8,
  input  _9,
  input  _0,
  output [3:0] out_11,
  output enable
);

  or or_1 (out_11[0], _1, _3, _5, _7, _9);
  or or_2 (out_11[1], _2, _3, _7, _6);
  or or_3 (out_11[2], _4, _5, _6, _7);
  or or_4 (out_11[3], _8, _9);
  or or_5 (enable, _1, _2, _3, _4, _5, _6, _7, _8, _9, _0);
endmodule
