// Logisim project COMP_8.circ as structural Verilog: 1 circuit, main circuit COMPARE_8
module COMPARE_8 (
  input  [7:0] A,
  input  [7:0] B,
  output A_2,
  output out_4,
  output B_2
);

  wire compare_1_1_out_4, compare_1_1_out_5, compare_1_1_out_6, compare_1_2_out_4, compare_1_2_out_5,
       compare_1_2_out_6, compare_1_3_out_4, compare_1_3_out_5, compare_1_3_out_6, compare_1_4_out_4,
       compare_1_4_out_5, compare_1_4_out_6, compare_1_5_out_4, compare_1_5_out_5, compare_1_5_out_6,
       compare_1_6_out_4, compare_1_6_out_5, compare_1_6_out_6, compare_1_7_out_4, compare_1_7_out_5,
       compare_1_7_out_6, compare_1_8_out_4, compare_1_8_out_6;

  COMPARE_1 compare_1_1 (
    .A(A[7]), .B(B[7]), .in_3(1'b1), .out_4(compare_1_1_out_4), .out_5(compare_1_1_out_5),
    .out_6(compare_1_1_out_6));
  COMPARE_1 compare_1_2 (
    .A(A[6]), .B(B[6]), .in_3(compare_1_1_out_5), .out_4(compare_1_2_out_4), .out_5(compare_1_2_out_5),
    .out_6(compare_1_2_out_6));
  COMPARE_1 compare_1_3 (
    .A(A[5]), .B(B[5]), .in_3(compare_1_2_out_5), .out_4(compare_1_3_out_4), .out_5(compare_1_3_out_5),
    .out_6(compare_1_3_out_6));
  COMPARE_1 compare_1_4 (
    .A(A[4]), .B(B[4]), .in_3(compare_1_3_out_5), .out_4(compare_1_4_out_4), .out_5(compare_1_4_out_5),
    .out_6(compare_1_4_out_6));
  COMPARE_1 compare_1_5 (
    .A(A[3]), .B(B[3]), .in_3(compare_1_4_out_5), .out_4(compare_1_5_out_4), .out_5(compare_1_5_out_5),
    .out_6(compare_1_5_out_6));
  COMPARE_1 compare_1_6 (
    .A(A[2]), .B(B[2]), .in_3(compare_1_5_out_5), .out_4(compare_1_6_out_4), .out_5(compare_1_6_out_5),
    .out_6(compare_1_6_out_6));
  COMPARE_1 compare_1_7 (
    .A(A[1]), .B(B[1]), .in_3(compare_1_6_out_5), .out_4(compare_1_7_out_4), .out_5(compare_1_7_out_5),
    .out_6(compare_1_7_out_6));
  COMPARE_1 compare_1_8 (
    .A(A[0]), .B(B[0]), .in_3(compare_1_7_out_5), .out_4(compare_1_8_out_4), .out_5(out_4),
    .out_6(compare_1_8_out_6));
  nand nand_1 (A_2, ~compare_1_1_out_4, ~compare_1_2_out_4, ~compare_1_3_out_4, ~compare_1_4_out_4, ~compare_1_5_out_4, ~compare_1_6_out_4, ~compare_1_7_out_4, ~compare_1_8_out_4);  // NAND_Gate
  nand nand_2 (B_2, ~compare_1_1_out_6, ~compare_1_2_out_6, ~compare_1_3_out_6, ~compare_1_4_out_6, ~compare_1_5_out_6, ~compare_1_6_out_6, ~compare_1_7_out_6, ~compare_1_8_out_6);  // NAND_Gate
endmodule
