// Logisim project COUNTER_2.circ as structural Verilog: 1 circuit, main circuit main
module main (
  input  clock,
  input  back,
  input  reset,
  output [1:0] out_4
);

  wire d_ff_1_qn, d_ff_2_qn, transistor_1_out;

  D_Flip_Flop d_ff_1 (.clk(clock), .D(d_ff_1_qn), .Q(out_4[0]), .Qn(d_ff_1_qn), .reset(reset));  // open: preset, en
  Transistor #(.\type ("n")) transistor_1 (.in(out_4[0]), .out(transistor_1_out), .gate(back));
  Transistor transistor_2 (.in(d_ff_1_qn), .out(transistor_1_out), .gate(back));
  D_Flip_Flop d_ff_2 (
    .clk(transistor_1_out), .D(d_ff_2_qn), .Q(out_4[1]), .Qn(d_ff_2_qn), .reset(reset));  // open: preset, en
endmodule
