// Logisim project DEC_TO_BIN.circ as structural Verilog: 1 circuit, main circuit DEC_TO_BIN
module DEC_TO_BIN (
  input  [3:0] value,
  input  enable,
  input  reset,
  output [7:0] out_value
);

  wire sum_8_1_out_4, sum_8_2_out_4;
  wire [3:0] rejestr_4_1_out_4, rejestr_4_2_out_4, rejestr_4_3_out_4;
  wire [7:0] sum_8_1_out_3, X10_out_3, X100_out_3;

  REJESTR_4 rejestr_4_1 (.in_1(value), .out_4(rejestr_4_1_out_4), .clc(enable), .reset(reset));
  REJESTR_4 rejestr_4_2 (.in_1(rejestr_4_1_out_4), .out_4(rejestr_4_2_out_4), .clc(enable), .reset(reset));
  REJESTR_4 rejestr_4_3 (.in_1(rejestr_4_2_out_4), .out_4(rejestr_4_3_out_4), .clc(enable), .reset(reset));
  MULTI_8 X10 (.in_1({4'b0000, rejestr_4_2_out_4}), .in_2(8'ha), .out_3(X10_out_3));
  MULTI_8 X100 (.in_1({4'b0000, rejestr_4_3_out_4}), .in_2(8'h64), .out_3(X100_out_3));
  SUM_8 sum_8_1 (.in_1({4'b0000, rejestr_4_1_out_4}), .in_2(X100_out_3), .out_3(sum_8_1_out_3), .out_4(sum_8_1_out_4));
  SUM_8 sum_8_2 (.in_1(sum_8_1_out_3), .in_2(X10_out_3), .out_3(out_value), .out_4(sum_8_2_out_4));
  // also tied to GND on the sheet: {sum_8_1_out_4, sum_8_2_out_4}
endmodule
