// Logisim project DIV_8v4.circ as structural Verilog: 1 circuit, main circuit DIV_8
module DIV_8 (
  input  [7:0] in_1,
  input  start,
  input  [7:0] in_3,
  output [7:0] out_4,
  output stop
);

  wire compare_8_1_out_4, del_comp_8_1_out, del_comp_8_2_out, del_comp_8_3_out, del_comp_8_4_out,
       del_comp_8_5_out, del_comp_8_6_out, del_comp_8_7_out, del_comp_8_8_out, del_comp_8_9_out, not_1_out,
       not_2_out, not_3_out, not_4_out, not_5_out, pu_3_reszta_out, \pu_3_równa_out , pu_4_reszta_out,
       \pu_4_równa_out , pu_5_reszta_out, \pu_5_równa_out , pu_7_reszta_out, pu_9_reszta_out,
       \pu_9_równa_out , pu_10_reszta_out, \pu_10_równa_out , pu_11_reszta_out, \pu_11_równa_out ,
       pu_12_reszta_out, \pu_12_równa_out , pu_13_reszta_out, \pu_13_równa_out , pu_14_reszta_out,
       \pu_14_równa_out , pu_15_reszta_out, \pu_15_równa_out , pu_16_reszta_out, \pu_16_równa_out ,
       pu_18_reszta_out, \pu_18_równa_out , pu_20_reszta_out, \pu_20_równa_out , pu_21_reszta_out,
       \pu_21_równa_out , pu_22_reszta_out, \pu_22_równa_out , pu_23_reszta_out, \pu_23_równa_out ,
       pu_24_reszta_out, \pu_24_równa_out , pu_25_reszta_out, \pu_25_równa_out , pu_26_reszta_out,
       \pu_26_równa_out , pu_27_reszta_out, \pu_27_równa_out , pu_28_reszta_out, \pu_28_równa_out ,
       pu_29_reszta_out, \pu_29_równa_out , pu_30_reszta_out, \pu_30_równa_out , \pu_32_równa_out ,
       pu_33_reszta_out, \pu_33_równa_out , pu_34_reszta_out, \pu_34_równa_out , pu_35_reszta_out,
       \pu_35_równa_out , pu_36_reszta_out, \pu_36_równa_out , pu_37_reszta_out, \pu_37_równa_out ,
       pu_38_reszta_out, \pu_38_równa_out , pu_39_reszta_out, \pu_39_równa_out , pu_40_reszta_out,
       \pu_40_równa_out , pu_41_reszta_out, \pu_41_równa_out , pu_42_reszta_out, \pu_42_równa_out ,
       pu_43_reszta_out, \pu_43_równa_out , pu_44_reszta_out, \pu_44_równa_out , \pu_45_równa_out ,
       pu_46_reszta_out, \pu_46_równa_out , pu_47_reszta_out, \pu_47_równa_out , pu_48_reszta_out,
       \pu_48_równa_out , pu_49_reszta_out, \pu_49_równa_out , pu_50_reszta_out, \pu_50_równa_out ,
       pu_51_reszta_out, \pu_51_równa_out , pu_52_reszta_out, \pu_52_równa_out , pu_53_reszta_out,
       \pu_53_równa_out , pu_54_reszta_out, \pu_54_równa_out , \pu_55_równa_out , \pu_56_równa_out ,
       pu_57_reszta_out, \pu_57_równa_out , pu_58_reszta_out, \pu_58_równa_out , pu_59_reszta_out,
       \pu_59_równa_out , pu_60_reszta_out, \pu_60_równa_out , pu_61_reszta_out, \pu_61_równa_out ,
       \pu_62_równa_out , \pu_63_równa_out , pu_64_reszta_out, \pu_64_równa_out , pu_65_reszta_out,
       \pu_65_równa_out , pu_66_reszta_out, \pu_66_równa_out , \pu_67_równa_out , \pu_68_równa_out ,
       transistor_3_out;
  wire [7:0] del_comp_8_1_var_2_out, del_comp_8_2_var_2_out, del_comp_8_3_var_2_out, del_comp_8_4_var_2_out,
       del_comp_8_5_var_2_out, del_comp_8_6_var_2_out, del_comp_8_7_var_2_out, del_comp_8_8_var_2_out,
       \pu_31_równa_out ;

  PU pu_1 (
    .\równa_out (\pu_31_równa_out [7]), .var_out(\pu_31_równa_out [7]), .\równa (\pu_3_równa_out ),
    .dzielnik(in_3[7]), .reszta(1'b0));  // open: reszta_out
  PU pu_2 (
    .\równa_out (\pu_31_równa_out [6]), .var_out(\pu_31_równa_out [6]), .\równa (\pu_5_równa_out ),
    .dzielnik(in_3[7]), .reszta(pu_3_reszta_out));  // open: reszta_out
  PU pu_3 (
    .\równa_out (\pu_3_równa_out ), .var_out(\pu_31_równa_out [7]), .\równa (\pu_4_równa_out ),
    .dzielnik(in_3[6]), .reszta(1'b0), .reszta_out(pu_3_reszta_out));
  PU pu_4 (
    .\równa_out (\pu_4_równa_out ), .var_out(\pu_31_równa_out [7]), .\równa (\pu_10_równa_out ),
    .dzielnik(in_3[5]), .reszta(1'b0), .reszta_out(pu_4_reszta_out));
  PU pu_5 (
    .\równa_out (\pu_5_równa_out ), .var_out(\pu_31_równa_out [6]), .\równa (\pu_12_równa_out ),
    .dzielnik(in_3[6]), .reszta(pu_4_reszta_out), .reszta_out(pu_5_reszta_out));
  PU pu_6 (
    .\równa_out (\pu_31_równa_out [5]), .var_out(\pu_31_równa_out [5]), .\równa (\pu_14_równa_out ),
    .dzielnik(in_3[7]), .reszta(pu_5_reszta_out));  // open: reszta_out
  PU pu_7 (
    .\równa_out (\pu_31_równa_out [4]), .var_out(\pu_31_równa_out [4]), .\równa (\pu_15_równa_out ),
    .dzielnik(in_3[7]), .reszta(pu_14_reszta_out), .reszta_out(pu_7_reszta_out));
  PU pu_8 (
    .\równa_out (\pu_31_równa_out [3]), .var_out(\pu_31_równa_out [3]), .\równa (\pu_16_równa_out ),
    .dzielnik(1'b0), .reszta(pu_7_reszta_out));  // open: reszta_out
  PU pu_9 (
    .\równa_out (\pu_9_równa_out ), .var_out(\pu_31_równa_out [7]), .\równa (\pu_20_równa_out ),
    .dzielnik(in_3[3]), .reszta(1'b0), .reszta_out(pu_9_reszta_out));
  PU pu_10 (
    .\równa_out (\pu_10_równa_out ), .var_out(\pu_31_równa_out [7]), .\równa (\pu_9_równa_out ),
    .dzielnik(in_3[4]), .reszta(1'b0), .reszta_out(pu_10_reszta_out));
  PU pu_11 (
    .\równa_out (\pu_11_równa_out ), .var_out(\pu_31_równa_out [6]), .\równa (\pu_21_równa_out ),
    .dzielnik(in_3[4]), .reszta(pu_9_reszta_out), .reszta_out(pu_11_reszta_out));
  PU pu_12 (
    .\równa_out (\pu_12_równa_out ), .var_out(\pu_31_równa_out [6]), .\równa (\pu_11_równa_out ),
    .dzielnik(in_3[5]), .reszta(pu_10_reszta_out), .reszta_out(pu_12_reszta_out));
  PU pu_13 (
    .\równa_out (\pu_13_równa_out ), .var_out(\pu_31_równa_out [5]), .\równa (\pu_23_równa_out ),
    .dzielnik(in_3[5]), .reszta(pu_11_reszta_out), .reszta_out(pu_13_reszta_out));
  PU pu_14 (
    .\równa_out (\pu_14_równa_out ), .var_out(\pu_31_równa_out [5]), .\równa (\pu_13_równa_out ),
    .dzielnik(in_3[6]), .reszta(pu_12_reszta_out), .reszta_out(pu_14_reszta_out));
  PU pu_15 (
    .\równa_out (\pu_15_równa_out ), .var_out(\pu_31_równa_out [4]), .\równa (\pu_25_równa_out ),
    .dzielnik(in_3[6]), .reszta(pu_13_reszta_out), .reszta_out(pu_15_reszta_out));
  PU pu_16 (
    .\równa_out (\pu_16_równa_out ), .var_out(\pu_31_równa_out [3]), .\równa (\pu_28_równa_out ),
    .dzielnik(in_3[7]), .reszta(pu_15_reszta_out), .reszta_out(pu_16_reszta_out));
  PU pu_17 (
    .\równa_out (\pu_31_równa_out [2]), .var_out(\pu_31_równa_out [2]), .\równa (\pu_18_równa_out ),
    .dzielnik(1'b0), .reszta(pu_16_reszta_out));  // open: reszta_out
  PU pu_18 (
    .\równa_out (\pu_18_równa_out ), .var_out(\pu_31_równa_out [2]), .\równa (\pu_29_równa_out ),
    .dzielnik(in_3[7]), .reszta(pu_28_reszta_out), .reszta_out(pu_18_reszta_out));
  PU pu_19 (
    .\równa_out (\pu_31_równa_out [1]), .var_out(\pu_31_równa_out [1]), .\równa (\pu_30_równa_out ),
    .dzielnik(1'b0), .reszta(pu_18_reszta_out));  // open: reszta_out
  PU pu_20 (
    .\równa_out (\pu_20_równa_out ), .var_out(\pu_31_równa_out [7]), .\równa (\pu_34_równa_out ),
    .dzielnik(in_3[2]), .reszta(1'b0), .reszta_out(pu_20_reszta_out));
  PU pu_21 (
    .\równa_out (\pu_21_równa_out ), .var_out(\pu_31_równa_out [6]), .\równa (\pu_22_równa_out ),
    .dzielnik(in_3[3]), .reszta(pu_20_reszta_out), .reszta_out(pu_21_reszta_out));
  PU pu_22 (
    .\równa_out (\pu_22_równa_out ), .var_out(\pu_31_równa_out [6]), .\równa (\pu_35_równa_out ),
    .dzielnik(in_3[2]), .reszta(pu_34_reszta_out), .reszta_out(pu_22_reszta_out));
  PU pu_23 (
    .\równa_out (\pu_23_równa_out ), .var_out(\pu_31_równa_out [5]), .\równa (\pu_24_równa_out ),
    .dzielnik(in_3[4]), .reszta(pu_21_reszta_out), .reszta_out(pu_23_reszta_out));
  PU pu_24 (
    .\równa_out (\pu_24_równa_out ), .var_out(\pu_31_równa_out [5]), .\równa (\pu_36_równa_out ),
    .dzielnik(in_3[3]), .reszta(pu_22_reszta_out), .reszta_out(pu_24_reszta_out));
  PU pu_25 (
    .\równa_out (\pu_25_równa_out ), .var_out(\pu_31_równa_out [4]), .\równa (\pu_26_równa_out ),
    .dzielnik(in_3[5]), .reszta(pu_23_reszta_out), .reszta_out(pu_25_reszta_out));
  PU pu_26 (
    .\równa_out (\pu_26_równa_out ), .var_out(\pu_31_równa_out [4]), .\równa (\pu_37_równa_out ),
    .dzielnik(in_3[4]), .reszta(pu_24_reszta_out), .reszta_out(pu_26_reszta_out));
  PU pu_27 (
    .\równa_out (\pu_27_równa_out ), .var_out(\pu_31_równa_out [3]), .\równa (\pu_40_równa_out ),
    .dzielnik(in_3[5]), .reszta(pu_26_reszta_out), .reszta_out(pu_27_reszta_out));
  PU pu_28 (
    .\równa_out (\pu_28_równa_out ), .var_out(\pu_31_równa_out [3]), .\równa (\pu_27_równa_out ),
    .dzielnik(in_3[6]), .reszta(pu_25_reszta_out), .reszta_out(pu_28_reszta_out));
  PU pu_29 (
    .\równa_out (\pu_29_równa_out ), .var_out(\pu_31_równa_out [2]), .\równa (\pu_41_równa_out ),
    .dzielnik(in_3[6]), .reszta(pu_27_reszta_out), .reszta_out(pu_29_reszta_out));
  PU pu_30 (
    .\równa_out (\pu_30_równa_out ), .var_out(\pu_31_równa_out [1]), .\równa (\pu_43_równa_out ),
    .dzielnik(in_3[7]), .reszta(pu_29_reszta_out), .reszta_out(pu_30_reszta_out));
  PU pu_31 (
    .\równa_out (\pu_31_równa_out [0]), .var_out(\pu_31_równa_out [0]), .\równa (\pu_32_równa_out ),
    .dzielnik(1'b0), .reszta(pu_30_reszta_out));  // open: reszta_out
  PU pu_32 (
    .\równa_out (\pu_32_równa_out ), .var_out(\pu_31_równa_out [0]), .\równa (\pu_45_równa_out ),
    .dzielnik(in_3[7]), .reszta(pu_43_reszta_out));  // open: reszta_out
  PU pu_33 (
    .\równa_out (\pu_33_równa_out ), .var_out(\pu_31_równa_out [7]), .\równa (1'b1), .dzielnik(in_3[0]),
    .reszta(in_1[7]), .reszta_out(pu_33_reszta_out));
  PU pu_34 (
    .\równa_out (\pu_34_równa_out ), .var_out(\pu_31_równa_out [7]), .\równa (\pu_33_równa_out ),
    .dzielnik(in_3[1]), .reszta(1'b0), .reszta_out(pu_34_reszta_out));
  PU pu_35 (
    .\równa_out (\pu_35_równa_out ), .var_out(\pu_31_równa_out [6]), .\równa (\pu_46_równa_out ),
    .dzielnik(in_3[1]), .reszta(pu_33_reszta_out), .reszta_out(pu_35_reszta_out));
  PU pu_36 (
    .\równa_out (\pu_36_równa_out ), .var_out(\pu_31_równa_out [5]), .\równa (\pu_47_równa_out ),
    .dzielnik(in_3[2]), .reszta(pu_35_reszta_out), .reszta_out(pu_36_reszta_out));
  PU pu_37 (
    .\równa_out (\pu_37_równa_out ), .var_out(\pu_31_równa_out [4]), .\równa (\pu_38_równa_out ),
    .dzielnik(in_3[3]), .reszta(pu_36_reszta_out), .reszta_out(pu_37_reszta_out));
  PU pu_38 (
    .\równa_out (\pu_38_równa_out ), .var_out(\pu_31_równa_out [4]), .\równa (\pu_49_równa_out ),
    .dzielnik(in_3[2]), .reszta(pu_47_reszta_out), .reszta_out(pu_38_reszta_out));
  PU pu_39 (
    .\równa_out (\pu_39_równa_out ), .var_out(\pu_31_równa_out [3]), .\równa (\pu_50_równa_out ),
    .dzielnik(in_3[3]), .reszta(pu_38_reszta_out), .reszta_out(pu_39_reszta_out));
  PU pu_40 (
    .\równa_out (\pu_40_równa_out ), .var_out(\pu_31_równa_out [3]), .\równa (\pu_39_równa_out ),
    .dzielnik(in_3[4]), .reszta(pu_37_reszta_out), .reszta_out(pu_40_reszta_out));
  PU pu_41 (
    .\równa_out (\pu_41_równa_out ), .var_out(\pu_31_równa_out [2]), .\równa (\pu_42_równa_out ),
    .dzielnik(in_3[5]), .reszta(pu_40_reszta_out), .reszta_out(pu_41_reszta_out));
  PU pu_42 (
    .\równa_out (\pu_42_równa_out ), .var_out(\pu_31_równa_out [2]), .\równa (\pu_52_równa_out ),
    .dzielnik(in_3[4]), .reszta(pu_39_reszta_out), .reszta_out(pu_42_reszta_out));
  PU pu_43 (
    .\równa_out (\pu_43_równa_out ), .var_out(\pu_31_równa_out [1]), .\równa (\pu_44_równa_out ),
    .dzielnik(in_3[6]), .reszta(pu_41_reszta_out), .reszta_out(pu_43_reszta_out));
  PU pu_44 (
    .\równa_out (\pu_44_równa_out ), .var_out(\pu_31_równa_out [1]), .\równa (\pu_54_równa_out ),
    .dzielnik(in_3[5]), .reszta(pu_42_reszta_out), .reszta_out(pu_44_reszta_out));
  PU pu_45 (
    .\równa_out (\pu_45_równa_out ), .var_out(\pu_31_równa_out [0]), .\równa (\pu_55_równa_out ),
    .dzielnik(in_3[6]), .reszta(pu_44_reszta_out));  // open: reszta_out
  PU pu_46 (
    .\równa_out (\pu_46_równa_out ), .var_out(\pu_31_równa_out [6]), .\równa (1'b1), .dzielnik(in_3[0]),
    .reszta(in_1[6]), .reszta_out(pu_46_reszta_out));
  PU pu_47 (
    .\równa_out (\pu_47_równa_out ), .var_out(\pu_31_równa_out [5]), .\równa (\pu_48_równa_out ),
    .dzielnik(in_3[1]), .reszta(pu_46_reszta_out), .reszta_out(pu_47_reszta_out));
  PU pu_48 (
    .\równa_out (\pu_48_równa_out ), .var_out(\pu_31_równa_out [5]), .\równa (1'b1), .dzielnik(in_3[0]),
    .reszta(in_1[5]), .reszta_out(pu_48_reszta_out));
  PU pu_49 (
    .\równa_out (\pu_49_równa_out ), .var_out(\pu_31_równa_out [4]), .\równa (\pu_57_równa_out ),
    .dzielnik(in_3[1]), .reszta(pu_48_reszta_out), .reszta_out(pu_49_reszta_out));
  PU pu_50 (
    .\równa_out (\pu_50_równa_out ), .var_out(\pu_31_równa_out [3]), .\równa (\pu_58_równa_out ),
    .dzielnik(in_3[2]), .reszta(pu_49_reszta_out), .reszta_out(pu_50_reszta_out));
  PU pu_51 (
    .\równa_out (\pu_51_równa_out ), .var_out(\pu_31_równa_out [2]), .\równa (\pu_60_równa_out ),
    .dzielnik(in_3[2]), .reszta(pu_58_reszta_out), .reszta_out(pu_51_reszta_out));
  PU pu_52 (
    .\równa_out (\pu_52_równa_out ), .var_out(\pu_31_równa_out [2]), .\równa (\pu_51_równa_out ),
    .dzielnik(in_3[3]), .reszta(pu_50_reszta_out), .reszta_out(pu_52_reszta_out));
  PU pu_53 (
    .\równa_out (\pu_53_równa_out ), .var_out(\pu_31_równa_out [1]), .\równa (\pu_61_równa_out ),
    .dzielnik(in_3[3]), .reszta(pu_51_reszta_out), .reszta_out(pu_53_reszta_out));
  PU pu_54 (
    .\równa_out (\pu_54_równa_out ), .var_out(\pu_31_równa_out [1]), .\równa (\pu_53_równa_out ),
    .dzielnik(in_3[4]), .reszta(pu_52_reszta_out), .reszta_out(pu_54_reszta_out));
  PU pu_55 (
    .\równa_out (\pu_55_równa_out ), .var_out(\pu_31_równa_out [0]), .\równa (\pu_56_równa_out ),
    .dzielnik(in_3[5]), .reszta(pu_54_reszta_out));  // open: reszta_out
  PU pu_56 (
    .\równa_out (\pu_56_równa_out ), .var_out(\pu_31_równa_out [0]), .\równa (\pu_63_równa_out ),
    .dzielnik(in_3[4]), .reszta(pu_53_reszta_out));  // open: reszta_out
  PU pu_57 (
    .\równa_out (\pu_57_równa_out ), .var_out(\pu_31_równa_out [4]), .\równa (1'b1), .dzielnik(in_3[0]),
    .reszta(in_1[4]), .reszta_out(pu_57_reszta_out));
  PU pu_58 (
    .\równa_out (\pu_58_równa_out ), .var_out(\pu_31_równa_out [3]), .\równa (\pu_59_równa_out ),
    .dzielnik(in_3[1]), .reszta(pu_57_reszta_out), .reszta_out(pu_58_reszta_out));
  PU pu_59 (
    .\równa_out (\pu_59_równa_out ), .var_out(\pu_31_równa_out [3]), .\równa (1'b1), .dzielnik(in_3[0]),
    .reszta(in_1[3]), .reszta_out(pu_59_reszta_out));
  PU pu_60 (
    .\równa_out (\pu_60_równa_out ), .var_out(\pu_31_równa_out [2]), .\równa (\pu_64_równa_out ),
    .dzielnik(in_3[1]), .reszta(pu_59_reszta_out), .reszta_out(pu_60_reszta_out));
  PU pu_61 (
    .\równa_out (\pu_61_równa_out ), .var_out(\pu_31_równa_out [1]), .\równa (\pu_66_równa_out ),
    .dzielnik(in_3[2]), .reszta(pu_60_reszta_out), .reszta_out(pu_61_reszta_out));
  PU pu_62 (
    .\równa_out (\pu_62_równa_out ), .var_out(\pu_31_równa_out [0]), .\równa (\pu_67_równa_out ),
    .dzielnik(in_3[2]), .reszta(pu_66_reszta_out));  // open: reszta_out
  PU pu_63 (
    .\równa_out (\pu_63_równa_out ), .var_out(\pu_31_równa_out [0]), .\równa (\pu_62_równa_out ),
    .dzielnik(in_3[3]), .reszta(pu_61_reszta_out));  // open: reszta_out
  PU pu_64 (
    .\równa_out (\pu_64_równa_out ), .var_out(\pu_31_równa_out [2]), .\równa (1'b1), .dzielnik(in_3[0]),
    .reszta(in_1[2]), .reszta_out(pu_64_reszta_out));
  PU pu_65 (
    .\równa_out (\pu_65_równa_out ), .var_out(\pu_31_równa_out [1]), .\równa (1'b1), .dzielnik(in_3[0]),
    .reszta(in_1[1]), .reszta_out(pu_65_reszta_out));
  PU pu_66 (
    .\równa_out (\pu_66_równa_out ), .var_out(\pu_31_równa_out [1]), .\równa (\pu_65_równa_out ),
    .dzielnik(in_3[1]), .reszta(pu_64_reszta_out), .reszta_out(pu_66_reszta_out));
  PU pu_67 (
    .\równa_out (\pu_67_równa_out ), .var_out(\pu_31_równa_out [0]), .\równa (\pu_68_równa_out ),
    .dzielnik(in_3[1]), .reszta(pu_65_reszta_out));  // open: reszta_out
  PU pu_68 (
    .\równa_out (\pu_68_równa_out ), .var_out(\pu_31_równa_out [0]), .\równa (1'b1), .dzielnik(in_3[0]),
    .reszta(in_1[0]));  // open: reszta_out
  not not_1 (not_1_out, start);
  COMPARE_8 compare_8_1 (.A(in_3), .B({8{1'b0}}), .out_4(compare_8_1_out_4));  // open: A_2, B_2
  not not_2 (not_2_out, not_1_out);
  Transistor #(.width(8)) transistor_1 (.in(\pu_31_równa_out ), .out(out_4), .gate(compare_8_1_out_4));
  Transistor #(.\type ("n"), .width(8)) transistor_2 (.in({8{1'b0}}), .out(out_4), .gate(compare_8_1_out_4));
  Del_comp_8 del_comp_8_1 (
    .var_2_in(out_4), .start(not_2_out), .var_2_out(del_comp_8_1_var_2_out), .out(del_comp_8_1_out));
  Del_comp_8 del_comp_8_2 (
    .var_2_in(del_comp_8_1_var_2_out), .start(del_comp_8_1_out), .var_2_out(del_comp_8_2_var_2_out),
    .out(del_comp_8_2_out), .in_1(out_4));
  Del_comp_8 del_comp_8_3 (
    .var_2_in(del_comp_8_2_var_2_out), .start(del_comp_8_2_out), .var_2_out(del_comp_8_3_var_2_out),
    .out(del_comp_8_3_out), .in_1(out_4));
  Del_comp_8 del_comp_8_4 (
    .var_2_in(del_comp_8_3_var_2_out), .start(del_comp_8_3_out), .var_2_out(del_comp_8_4_var_2_out),
    .out(del_comp_8_4_out), .in_1(out_4));
  Del_comp_8 del_comp_8_5 (
    .var_2_in(del_comp_8_4_var_2_out), .start(del_comp_8_4_out), .var_2_out(del_comp_8_5_var_2_out),
    .out(del_comp_8_5_out), .in_1(out_4));
  Del_comp_8 del_comp_8_6 (
    .var_2_in(del_comp_8_5_var_2_out), .start(del_comp_8_5_out), .var_2_out(del_comp_8_6_var_2_out),
    .out(del_comp_8_6_out), .in_1(out_4));
  Del_comp_8 del_comp_8_7 (
    .var_2_in(del_comp_8_6_var_2_out), .start(del_comp_8_6_out), .var_2_out(del_comp_8_7_var_2_out),
    .out(del_comp_8_7_out), .in_1(out_4));
  Del_comp_8 del_comp_8_8 (
    .var_2_in(del_comp_8_7_var_2_out), .start(del_comp_8_7_out), .var_2_out(del_comp_8_8_var_2_out),
    .out(del_comp_8_8_out), .in_1(out_4));
  Del_comp_8 del_comp_8_9 (
    .var_2_in(del_comp_8_8_var_2_out), .start(del_comp_8_8_out), .out(del_comp_8_9_out), .in_1(out_4));  // open: var_2_out
  Transistor transistor_3 (.in(1'b0), .out(transistor_3_out), .gate(del_comp_8_9_out));
  Transistor #(.\type ("n")) transistor_4 (.in(not_2_out), .out(transistor_3_out), .gate(del_comp_8_9_out));
  Counter counter_1 (.clk(del_comp_8_9_out));  // open: load, D, count, Q, carry, clr
  not not_3 (not_3_out, not_4_out);
  not not_4 (not_4_out, transistor_3_out);
  not not_5 (not_5_out, not_3_out);
  not not_6 (stop, not_5_out);

  // Other names for the same wires on the sheet: div[7:0] = in_3
endmodule
