// Logisim project Del_comp_8_2inputs.circ as structural Verilog: 1 circuit, main circuit Del_comp_8
module Del_comp_8 (
  input  [7:0] in_1,
  input  [7:0] var_2_in,
  input  start,
  output [7:0] var_2_out,
  output out
);

  wire and_1_out, compare_8_1_a_2, compare_8_1_b_2, compare_8_1_out_4, not_1_out, not_2_out, not_3_out,
       not_4_out;
  wire [7:0] transistor_1_out, transistor_2_out, transistor_18_out, transistor_20_out;

  Transistor #(.\type ("n"), .gate("br"), .width(8)) transistor_1 (.in(var_2_in), .out(transistor_1_out), .gate(start));
  Transistor #(.\type ("n")) transistor_2 (
    .in(transistor_1_out[0]), .out(transistor_2_out[0]), .gate(transistor_1_out[0]));
  Transistor #(.\type ("n")) transistor_3 (
    .in(transistor_1_out[1]), .out(transistor_2_out[1]), .gate(transistor_1_out[1]));
  Transistor #(.\type ("n")) transistor_4 (
    .in(transistor_1_out[2]), .out(transistor_2_out[2]), .gate(transistor_1_out[2]));
  Transistor #(.\type ("n")) transistor_5 (
    .in(transistor_1_out[3]), .out(transistor_2_out[3]), .gate(transistor_1_out[3]));
  Transistor #(.\type ("n")) transistor_6 (
    .in(transistor_1_out[4]), .out(transistor_2_out[4]), .gate(transistor_1_out[4]));
  Transistor #(.\type ("n")) transistor_7 (
    .in(transistor_1_out[5]), .out(transistor_2_out[5]), .gate(transistor_1_out[5]));
  Transistor #(.\type ("n")) transistor_8 (
    .in(transistor_1_out[6]), .out(transistor_2_out[6]), .gate(transistor_1_out[6]));
  Transistor #(.\type ("n")) transistor_9 (
    .in(transistor_1_out[7]), .out(transistor_2_out[7]), .gate(transistor_1_out[7]));
  Transistor transistor_10 (.in(1'b0), .out(transistor_2_out[0]), .gate(transistor_1_out[0]));
  Transistor transistor_11 (.in(1'b0), .out(transistor_2_out[3]), .gate(transistor_1_out[3]));
  Transistor transistor_12 (.in(1'b0), .out(transistor_2_out[1]), .gate(transistor_1_out[1]));
  Transistor transistor_13 (.in(1'b0), .out(transistor_2_out[2]), .gate(transistor_1_out[2]));
  Transistor transistor_14 (.in(1'b0), .out(transistor_2_out[5]), .gate(transistor_1_out[5]));
  Transistor transistor_15 (.in(1'b0), .out(transistor_2_out[6]), .gate(transistor_1_out[6]));
  Transistor transistor_16 (.in(1'b0), .out(transistor_2_out[4]), .gate(transistor_1_out[4]));
  not not_1 (not_1_out, not_2_out);
  not not_2 (not_2_out, start);
  Transistor transistor_17 (.in(1'b0), .out(transistor_2_out[7]), .gate(transistor_1_out[7]));
  Transistor #(.gate("br"), .width(8)) transistor_18 (.in({8{1'b0}}), .out(transistor_18_out), .gate(not_1_out));
  Transistor #(.\type ("n"), .gate("br"), .width(8)) transistor_19 (
    .in(transistor_2_out), .out(transistor_18_out), .gate(not_1_out));
  Transistor #(.width(8)) transistor_20 (.in({8{1'b1}}), .out(transistor_20_out), .gate(not_1_out));
  Transistor #(.\type ("n"), .width(8)) transistor_21 (.in(in_1), .out(transistor_20_out), .gate(not_1_out));
  COMPARE_8 compare_8_1 (
    .A(transistor_20_out), .B(transistor_18_out), .A_2(compare_8_1_a_2), .out_4(compare_8_1_out_4),
    .B_2(compare_8_1_b_2));
  not not_3 (not_3_out, compare_8_1_a_2);
  and and_1 (and_1_out, not_3_out, compare_8_1_out_4, not_4_out);
  not not_4 (not_4_out, compare_8_1_b_2);
  Transistor transistor_22 (.in(1'b0), .out(out), .gate(start));
  Transistor #(.\type ("n"), .gate("br")) transistor_23 (.in(and_1_out), .out(out), .gate(start));

  assign var_2_out = in_1;
endmodule
