// Logisim project EXTRA_DISP.circ as structural Verilog: 1 circuit, main circuit EXTRA_DIPS
module EXTRA_DIPS (
  input  in_1,
  input  in_2,
  input  x,
  input  in_4,
  input  pier,
  input  in_6,
  input  M,
  input  in_8,
  input  in_9,
  input  in_10,
  input  Reset,
  input  minus,
  output [4:0] LO1,
  output [4:0] O2,
  output [4:0] O3,
  output [4:0] O4,
  output [4:0] O5,
  output _71,
  output _72,
  output _73,
  output _74,
  output _75,
  output _76,
  output _77,
  output _78
);

  wire d_ff_1_q, d_ff_2_q, d_ff_3_q, d_ff_4_q, d_ff_5_q, d_ff_6_q, d_ff_7_q, d_ff_8_q, d_ff_9_q, d_ff_10_q,
       or_1_out;
  wire [3:0] or_2_out;

  or or_1 (or_1_out, in_1, in_2, x, in_4, pier, in_6, M, in_8, in_9, in_10);
  D_Flip_Flop d_ff_1 (.clk(or_1_out), .D(in_1), .Q(d_ff_1_q), .reset(Reset));  // open: Qn, preset, en
  D_Flip_Flop d_ff_2 (.clk(or_1_out), .D(in_2), .Q(d_ff_2_q), .reset(Reset));  // open: Qn, preset, en
  D_Flip_Flop d_ff_3 (.clk(or_1_out), .D(x), .Q(d_ff_3_q), .reset(Reset));  // open: Qn, preset, en
  D_Flip_Flop d_ff_4 (.clk(or_1_out), .D(in_4), .Q(d_ff_4_q), .reset(Reset));  // open: Qn, preset, en
  D_Flip_Flop d_ff_5 (.clk(or_1_out), .D(pier), .Q(d_ff_5_q), .reset(Reset));  // open: Qn, preset, en
  D_Flip_Flop d_ff_6 (.clk(or_1_out), .D(in_6), .Q(d_ff_6_q), .reset(Reset));  // open: Qn, preset, en
  D_Flip_Flop d_ff_7 (.clk(or_1_out), .D(M), .Q(d_ff_7_q), .reset(Reset));  // open: Qn, preset, en
  D_Flip_Flop d_ff_8 (.clk(or_1_out), .D(in_8), .Q(d_ff_8_q), .reset(Reset));  // open: Qn, preset, en
  D_Flip_Flop d_ff_9 (.clk(or_1_out), .D(in_9), .Q(d_ff_9_q), .reset(Reset));  // open: Qn, preset, en
  D_Flip_Flop d_ff_10 (.clk(or_1_out), .D(in_10), .Q(d_ff_10_q), .reset(Reset));  // open: Qn, preset, en
  or or_2 (or_2_out[0], d_ff_1_q, d_ff_3_q, d_ff_5_q, d_ff_7_q, d_ff_9_q);
  or or_3 (or_2_out[1], d_ff_2_q, d_ff_3_q, d_ff_6_q, d_ff_7_q, d_ff_10_q);
  or or_4 (or_2_out[2], d_ff_4_q, d_ff_5_q, d_ff_6_q, d_ff_7_q);
  or or_5 (or_2_out[3], d_ff_8_q, d_ff_9_q, d_ff_10_q);
  ROM #(.addrWidth(4), .dataWidth(25)) rom_1 (.addr(or_2_out), .data({O5, O4, O3, O2, LO1}));  // open: sel
  DotMatrix #(.matrixrows(5)) dotmatrix_1 (.col0(O5), .col1(O4), .col2(O3), .col3(O2), .col4(LO1));

  assign _71 = 1'b0;
  assign _72 = 1'b0;
  assign _73 = 1'b0;
  assign _74 = 1'b0;
  assign _75 = minus;
  assign _76 = 1'b0;
  assign _77 = 1'b0;
  assign _78 = 1'b0;

  // Notes on the sheet:
  //   contents of rom_1 (hex, n*v repeats v):
  //   0 23880 21080 1151151 111110 4107d0 1111111 1f4111f 111110
endmodule
