// Logisim project HSUM.circ as structural Verilog: 1 circuit, main circuit HSUM
module HSUM (
  input  X,
  input  Y,
  output Sum,
  output Carry
);

  xor xor_1 (Sum, X, Y);
  and and_1 (Carry, X, Y);
endmodule
