// Logisim project INTERFACE.circ as structural Verilog: 1 circuit, main circuit INTERFACE
module INTERFACE (
);

  wire _0, _1, _2, _3, _4, _5, _6, _7, _8, _9, _71, _72, _73, _74, _75, _76, _77, _78, AL, AM, b1, b2, b3,
       b4, b5, b6, b7, b8, C, CANCEL, CLEAR_MEM, COMP, LOAD, M, m1, m2, m3, m4, m5, m6, m7, m8, main_1_neg,
       ML, n1, n2, n3, n4, n5, n6, n7, n8, or_1_out, SAVE, tunnel, tunnel_t, tunnel_t_t, tunnel_t_t_t,
       tunnel_t_t_t_t, tunnel_t_t_t_t_t, tunnel_t_t_t_t_t_t, tunnel_t_t_t_t_t_t_t, tunnel_t_t_t_t_t_t_t_t,
       tunnel_t_t_t_t_t_t_t_t_t, v, x;
  wire [4:0] s1, s2, s3, s4, s5;

  DotMatrix #(.matrixrows(5)) dotmatrix_1 (.col0(s1), .col1(s2), .col2(s3), .col3(s4), .col4(s5));
  Button button (.out(tunnel_t_t_t_t_t));
  Button u__1 (.out(_1));
  Button u__4 (.out(_4));
  Button u__7 (.out(_7));
  Button u__0 (.out(_0));
  _7_Segment_Display u_7_segment_display_1 (.g(_75), .f(_76), .a(_77), .b(_78), .e(_71), .d(_72), .c(_73), .dp(_74));
  Button button_2 (.out(tunnel_t_t_t_t_t_t_t));
  Button u__2 (.out(_2));
  Button u__5 (.out(_5));
  Button u__8 (.out(_8));
  Button button_3 (.out(tunnel_t_t));
  MAIN_main main_1 (
    ._1(_1), ._2(_2), ._3(_3), ._4(_4), ._5(_5), ._6(_6), ._7(_7), ._8(_8), ._9(_9), ._0(_0),
    .in_11(tunnel_t), .in_12(tunnel_t_t_t), .x(x), .in_14(tunnel_t_t_t_t), .in_15(tunnel),
    .in_16(tunnel_t_t_t_t_t_t_t_t_t), .in_17(tunnel_t_t_t_t_t_t), .C(C), .in_19(tunnel_t_t_t_t_t),
    .in_20(tunnel_t_t_t_t_t_t_t), .in_21(tunnel_t_t_t_t_t_t_t_t), .v(v), .load(LOAD), .save(SAVE), .M(M),
    .AnsMem(AM), .clr_mem(CLEAR_MEM), .anuluj(CANCEL), .in_29(tunnel_t_t), .n1(n1), .n2(n2), .n3(n3),
    .n4(n4), .n5(n5), .n6(n6), .n7(n7), .n8(n8), .m1(m1), .m2(m2), .m3(m3), .m4(m4), .m5(m5), .m6(m6),
    .m7(m7), .m8(m8), .b1(b1), .b2(b2), .b3(b3), .b4(b4), .b5(b5), .b6(b6), .b7(b7), .b8(b8), .MEM_LED(ML),
    .MEM_ANS_LED(AL), .STATE_LED(COMP), .NEG(main_1_neg));
  _7_Segment_Display u_7_segment_display_2 (.g(m5), .f(m6), .a(m7), .b(m8), .e(m1), .d(m2), .c(m3), .dp(m4));
  _7_Segment_Display u_7_segment_display_3 (.g(b5), .f(b6), .a(b7), .b(b8), .e(b1), .d(b2), .c(b3), .dp(b4));
  Button button_4 (.out(tunnel_t_t_t_t_t_t_t_t_t));
  Button u__3 (.out(_3));
  Button u__6 (.out(_6));
  Button u__9 (.out(_9));
  Button button_5 (.out(tunnel_t_t_t_t_t_t));
  _7_Segment_Display u_7_segment_display_4 (.g(n5), .f(n6), .a(n7), .b(n8), .e(n1), .d(n2), .c(n3), .dp(n4));
  Button button_6 (.out(tunnel));
  Button button_7 (.out(tunnel_t_t_t_t));
  Button u_x (.out(x));
  Button button_8 (.out(tunnel_t_t_t));
  Button button_9 (.out(tunnel_t));
  Button u_C (.out(C));
  Button button_10 (.out(tunnel_t_t_t_t_t_t_t_t));
  Button u_v (.out(v));
  Button u_Load (.out(LOAD));
  Button u_Cancel (.out(CANCEL));
  or or_1 (or_1_out, M, AM);
  LED Ans_Memory (.in(AL));
  LED User_Memory (.in(ML));
  LED Computing (.in(COMP));
  Button Memory (.out(M));
  Button Ans_Memory_2 (.out(AM));
  Button u_Save (.out(SAVE));
  Button Clear_Memory (.out(CLEAR_MEM));
  EXTRA_DIPS extra_dips_1 (
    .in_1(tunnel_t), .in_2(tunnel_t_t_t), .x(x), .in_4(tunnel_t_t_t_t), .pier(tunnel_t_t_t_t_t_t_t_t_t),
    .in_6(tunnel), .M(or_1_out), .in_8(tunnel_t_t_t_t_t), .in_9(tunnel_t_t_t_t_t_t_t),
    .in_10(tunnel_t_t_t_t_t_t), .Reset(C), .minus(main_1_neg), .LO1(s5), .O2(s4), .O3(s3), .O4(s2), .O5(s1),
    ._71(_71), ._72(_72), ._73(_73), ._74(_74), ._75(_75), ._76(_76), ._77(_77), ._78(_78));

  // Notes on the sheet:
  //   W razie wystąpienia oscylacji należy wcisnąć CTRL + E
  //   W przypadku gdy układ podaje zły wynik i pali się ciągle dioda Computing należy wejść i zresetować modół który daje zwarcie/stan nie określony na pin "Stop"
endmodule
