// Logisim project MAIN.circ as structural Verilog: 1 circuit, main circuit main
module main (
  input  _1,
  input  _2,
  input  _3,
  input  _4,
  input  _5,
  input  _6,
  input  _7,
  input  _8,
  input  _9,
  input  _0,
  input  in_11,
  input  in_12,
  input  x,
  input  in_14,
  input  in_15,
  input  in_16,
  input  in_17,
  input  C,
  input  in_19,
  input  in_20,
  input  in_21,
  input  v,
  input  load,
  input  save,
  input  M,
  input  AnsMem,
  input  clr_mem,
  input  anuluj,
  input  in_29,
  output n1,
  output n2,
  output n3,
  output n4,
  output n5,
  output n6,
  output n7,
  output n8,
  output m1,
  output m2,
  output m3,
  output m4,
  output m5,
  output m6,
  output m7,
  output m8,
  output b1,
  output b2,
  output b3,
  output b4,
  output b5,
  output b6,
  output b7,
  output b8,
  output MEM_LED,
  output MEM_ANS_LED,
  output STATE_LED,
  output NEG
);

  wire and_2_out, cl, CLEAR, compare_8_1_a_2, compare_8_1_b_2, d_ff_1_qn, d_ff_4_q, d_ff_5_q, d_ff_7_q,
       d_ff_8_q, d_ff_9_q, data_in_neg, en, enable, ld, mem_in_neg, mem_out_neg, MEM_VAL_OUT_NEG,
       mod_selection_1_change, not_1_out, or_1_out, or_4_out, or_5_out, or_6_out, or_7_out, or_9_out,
       or_10_out, or_11_out, or_12_out, or_13_out, or_14_out, or_15_out, or_16_out, or_18_out, or_21_out,
       or_22_out, or_23_out, or_24_out, or_25_out, or_26_out, or_27_out, ram_1_data, sel, str, tunnel_t_t,
       tunnel_t_t_t_t_t_t, VAL_OUT_NEG;
  wire [1:0] Adres, main_1_out_4;
  wire [2:0] transistor_1_out, transistor_3_out;
  wire [3:0] but_to_bin_1_out_11;
  wire [7:0] data_in, data_out, mem_in, mem_out, MEM_VAL_OUT, ram_2_data, rejestr_8_1_out_4, VAL_IN, VAL_OUT;

  or or_1 (or_1_out, anuluj, C);
  or or_2 (tunnel_t_t_t_t_t_t, in_16, in_17);
  or or_3 (CLEAR, or_4_out, or_4_out, or_4_out);
  or or_4 (or_4_out, load, or_1_out, save);
  D_Flip_Flop d_ff_1 (
    .clk(in_29), .D(d_ff_1_qn), .Q(tunnel_t_t), .Qn(d_ff_1_qn), .reset(mod_selection_1_change));  // open: preset, en
  or or_5 (or_5_out, in_21, v);
  D_Flip_Flop d_ff_2 (.clk(M), .D(M), .Q(MEM_LED), .reset(or_6_out));  // open: Qn, preset, en
  or or_6 (or_6_out, CLEAR, AnsMem);
  D_Flip_Flop d_ff_3 (.clk(AnsMem), .D(AnsMem), .Q(MEM_ANS_LED), .reset(or_7_out));  // open: Qn, preset, en
  or or_7 (or_7_out, CLEAR, M);
  BUT_TO_BIN but_to_bin_1 (
    ._3(_3), ._2(_2), ._1(_1), ._6(_6), ._5(_5), ._4(_4), ._9(_9), ._8(_8), ._7(_7), ._0(_0),
    .out_11(but_to_bin_1_out_11), .enable(en));
  D_Flip_Flop d_ff_4 (.clk(v), .D(v), .Q(d_ff_4_q), .reset(in_21));  // open: Qn, preset, en
  COUNTER_2_main main_1 (.clock(tunnel_t_t_t_t_t_t), .back(1'b0), .reset(1'b0), .out_4(main_1_out_4));
  or or_8 (enable, en, or_9_out);
  DEC_TO_BIN dec_to_bin_1 (.value(but_to_bin_1_out_11), .enable(en), .reset(or_9_out), .out_value(VAL_IN));
  or or_9 (or_9_out, in_20, in_19, in_15, tunnel_t_t_t_t_t_t, in_14, x, in_12, in_11, C, in_16);
  COUNTER_2_main main_2 (.clock(or_5_out), .back(d_ff_4_q), .reset(or_1_out), .out_4(Adres));
  or or_10 (or_10_out, and_2_out, and_2_out, and_2_out);
  or or_11 (or_11_out, or_10_out, or_10_out, or_10_out);
  or or_12 (or_12_out, or_11_out, or_11_out, or_11_out);
  or or_13 (or_13_out, or_12_out, or_12_out, or_12_out);
  or or_14 (or_14_out, or_13_out, or_13_out, or_13_out);
  or or_15 (or_15_out, or_14_out, or_14_out, or_14_out);
  or or_16 (or_16_out, or_15_out, save);
  not not_1 (not_1_out, MEM_ANS_LED);
  or or_17 (sel, MEM_LED, tunnel_t_t_t_t_t_t, MEM_ANS_LED);
  and and_1 (str, or_16_out, not_1_out);
  or or_18 (or_18_out, or_16_out, or_16_out);
  Transistor #(.width(3)) transistor_1 (.in({MEM_ANS_LED, Adres}), .out(transistor_1_out), .gate(tunnel_t_t_t_t_t_t));
  Transistor #(.\type ("n"), .gate("br"), .width(3)) transistor_2 (
    .in({1'b1, main_1_out_4}), .out(transistor_1_out), .gate(tunnel_t_t_t_t_t_t));
  Transistor #(.width(3)) transistor_3 (.in({MEM_ANS_LED, Adres}), .out(transistor_3_out), .gate(tunnel_t_t_t_t_t_t));
  Transistor #(.\type ("n"), .gate("br"), .width(3)) transistor_4 (
    .in({1'b1, main_1_out_4}), .out(transistor_3_out), .gate(tunnel_t_t_t_t_t_t));
  Transistor #(.gate("br"), .width(8)) transistor_5 (.in(data_in), .out(mem_in), .gate(MEM_ANS_LED));
  MOD_SELECTION mod_selection_1 (
    .Disp(data_in), .pier(in_16), .VAL_IN(VAL_OUT), .CLEAR(C), .in_5(in_11), .in_6(in_12), .x(x),
    .in_8(in_14), .in_10(tunnel_t_t_t_t_t_t), .in_11(in_19), .in_12(in_20), .eneble(en), .in_13(in_15),
    .comp(STATE_LED), .in_2(VAL_OUT_NEG), .disp_neg(data_in_neg), .Change(mod_selection_1_change));  // open: ans
  or or_19 (cl, or_18_out, or_18_out);
  or or_20 (ld, sel, load);
  Transistor #(.gate("br")) transistor_6 (.in(data_in_neg), .out(mem_in_neg), .gate(MEM_ANS_LED));
  REJESTR_8 rejestr_8_1 (.in_1(mem_in), .out_4(rejestr_8_1_out_4), .clc(tunnel_t_t_t_t_t_t), .reset(enable));
  or or_21 (or_21_out, MEM_ANS_LED, MEM_LED);
  RAM #(.addrWidth(3), .dataWidth(1), .bus("separate")) ram_1 (
    .addr(transistor_1_out), .din(mem_in_neg), .data(ram_1_data), .str(str), .sel(sel), .clk(cl), .ld(ld),
    .clr(clr_mem));
  RAM #(.addrWidth(3), .bus("separate")) ram_2 (
    .addr(transistor_3_out), .din(mem_in), .data(ram_2_data), .str(str), .sel(sel), .clk(cl), .ld(ld),
    .clr(clr_mem));
  COMPARE_8 compare_8_1 (
    .A(rejestr_8_1_out_4), .B(mem_in), .A_2(compare_8_1_a_2), .B_2(compare_8_1_b_2));  // open: out_4
  or or_22 (or_22_out, compare_8_1_a_2, compare_8_1_b_2);
  and and_2 (and_2_out, tunnel_t_t_t_t_t_t, or_22_out);
  Transistor #(.width(8)) transistor_7 (.in(data_in), .out(mem_in), .gate(MEM_LED));
  Transistor #(.width(8)) transistor_8 (.in(data_in), .out(data_out), .gate(d_ff_5_q));
  D_Flip_Flop d_ff_5 (.clk(or_21_out), .D(or_21_out), .Q(d_ff_5_q), .reset(or_23_out));  // open: Qn, preset, en
  Transistor #(.\type ("n"), .width(8)) transistor_9 (.in(mem_out), .out(data_out), .gate(d_ff_5_q));
  or or_23 (or_23_out, enable, CLEAR);
  or or_24 (or_24_out, MEM_LED, MEM_ANS_LED);
  Transistor #(.\type ("n")) transistor_10 (.in(ram_1_data), .out(mem_out_neg), .gate(or_24_out));
  Transistor transistor_11 (.in(1'b0), .out(mem_out_neg), .gate(or_24_out));
  or or_25 (or_25_out, MEM_LED, MEM_ANS_LED);
  Transistor #(.\type ("n"), .width(8)) transistor_12 (.in(ram_2_data), .out(mem_out), .gate(or_25_out));
  Transistor #(.width(8)) transistor_13 (.in({8{1'b0}}), .out(mem_out), .gate(or_25_out));
  D_Flip_Flop d_ff_6 (.clk(load), .D(mem_out_neg), .Q(MEM_VAL_OUT_NEG));  // open: Qn, preset, en, reset
  REJESTR_8 rejestr_8_2 (.in_1(mem_out), .out_4(MEM_VAL_OUT), .clc(load));  // open: reset
  D_Flip_Flop d_ff_7 (.clk(load), .D(load), .Q(d_ff_7_q), .reset(mod_selection_1_change));  // open: Qn, preset, en
  Transistor #(.width(8)) transistor_14 (.in(VAL_IN), .out(VAL_OUT), .gate(d_ff_7_q));
  Transistor #(.\type ("n"), .width(8)) transistor_15 (.in(MEM_VAL_OUT), .out(VAL_OUT), .gate(d_ff_7_q));
  ROM #(.dataWidth(24)) rom_1 (
    .addr(data_out),
    .data({b8, b7, b6, b5, b4, b3, b2, b1, m8, m7, m6, m5, m4, m3, m2, m1, n8, n7, n6, n5, n4, n3, n2, n1}));  // open: sel
  Transistor transistor_16 (.in(data_in_neg), .out(mem_in_neg), .gate(MEM_LED));
  or or_26 (or_26_out, MEM_ANS_LED, MEM_LED);
  or or_27 (or_27_out, enable, CLEAR);
  Transistor transistor_17 (.in(data_in_neg), .out(NEG), .gate(d_ff_8_q));
  D_Flip_Flop d_ff_8 (.clk(or_26_out), .D(or_26_out), .Q(d_ff_8_q), .reset(or_27_out));  // open: Qn, preset, en
  Transistor #(.\type ("n")) transistor_18 (.in(mem_out_neg), .out(NEG), .gate(d_ff_8_q));
  D_Flip_Flop d_ff_9 (.clk(load), .D(load), .Q(d_ff_9_q), .reset(mod_selection_1_change));  // open: Qn, preset, en
  Transistor transistor_19 (.in(tunnel_t_t), .out(VAL_OUT_NEG), .gate(d_ff_9_q));
  Transistor #(.\type ("n")) transistor_20 (.in(MEM_VAL_OUT_NEG), .out(VAL_OUT_NEG), .gate(d_ff_9_q));

  // Other names for the same wires on the sheet: Adres[2] = MEM_ANS_LED; AM = MEM_ANS_LED; clr = clr_mem;
  //   data_out_neg = NEG; M_t = MEM_LED; MOVE = in_21; pier = in_16; tunnel = in_15; tunnel_t = in_11;
  //   tunnel_t_t_t = in_12; tunnel_t_t_t_t = in_14; tunnel_t_t_t_t_t = in_19; tunnel_t_t_t_t_t_t_t = in_20

  // Notes on the sheet:
  //   contents of rom_1 (hex, n*v repeats v):
  //   e7 84 d3 d6 b4 76 77 c4 f7 f6 84e7 8484 84d3 84d6 84b4 8476 8477 84c4 84f7 84f6 d3e7 d384 d3d3 d3d6
  //   d3b4 d376 d377 d3c4 d3f7 d3f6 d6e7 d684 d6d3 d6d6 d6b4 d676 d677 d6c4 d6f7 d6f6 b4e7 b484 b4d3 b4d6
  //   b4b4 b476 b477 b4c4 b4f7 b4f6 76e7 7684 76d3 76d6 76b4 7676 7677 76c4 76f7 76f6 77e7 7784 77d3 77d6
  //   77b4 7776 7777 77c4 77f7 77f6 c4e7 c484 c4d3 c4d6 c4b4 c476 c477 c4c4 c4f7 c4f6 f7e7 f784 f7d3 f7d6
  //   f7b4 f776 f777 f7c4 f7f7 f7f6 f6e7 f684 f6d3 f6d6 f6b4 f676 f677 f6c4 f6f7 f6f6 84e7e7 84e784 84e7d3
  //   84e7d6 84e7b4 84e776 84e777 84e7c4 84e7f7 84e7f6 8484e7 848484 8484d3 8484d6 8484b4 848476 848477
  //   8484c4 8484f7 8484f6 84d3e7 84d384 84d3d3 84d3d6 84d3b4 84d376 84d377 84d3c4 84d3f7 84d3f6 84d6e7
  //   84d684 84d6d3 84d6d6 84d6b4 84d676 84d677 84d6c4 84d6f7 84d6f6 84b4e7 84b484 84b4d3 84b4d6 84b4b4
  //   84b476 84b477 84b4c4 84b4f7 84b4f6 8476e7 847684 8476d3 8476d6 8476b4 847676 847677 8476c4 8476f7
  //   8476f6 8477e7 847784 8477d3 8477d6 8477b4 847776 847777 8477c4 8477f7 8477f6 84c4e7 84c484 84c4d3
  //   84c4d6 84c4b4 84c476 84c477 84c4c4 84c4f7 84c4f6 84f7e7 84f784 84f7d3 84f7d6 84f7b4 84f776 84f777
  //   84f7c4 84f7f7 84f7f6 84f6e7 84f684 84f6d3 84f6d6 84f6b4 84f676 84f677 84f6c4 84f6f7 84f6f6 d3e7e7
  //   d3e784 d3e7d3 d3e7d6 d3e7b4 d3e776 d3e777 d3e7c4 d3e7f7 d3e7f6 d384e7 d38484 d384d3 d384d6 d384b4
  //   d38476 d38477 d384c4 d384f7 d384f6 d3d3e7 d3d384 d3d3d3 d3d3d6 d3d3b4 d3d376 d3d377 d3d3c4 d3d3f7
  //   d3d3f6 d3d6e7 d3d684 d3d6d3 d3d6d6 d3d6b4 d3d676 d3d677 d3d6c4 d3d6f7 d3d6f6 d3b4e7 d3b484 d3b4d3
  //   d3b4d6 d3b4b4 d3b476 d3b477 d3b4c4 d3b4f7 d3b4f6 d37684 d37684 d376d3 d376d6 d376b4 d37676
endmodule
