// Logisim project MOD_CHOSEv3.circ as structural Verilog: 1 circuit, main circuit MOD_SELECTION
module MOD_SELECTION (
  input  [7:0] VAL_IN,
  input  in_2,
  input  eneble,
  input  CLEAR,
  input  in_5,
  input  in_6,
  input  x,
  input  in_8,
  input  pier,
  input  in_10,
  input  in_11,
  input  in_12,
  input  in_13,
  output [7:0] Disp,
  output disp_neg,
  output [7:0] ans,
  output Change,
  output comp
);

  wire _3, _4, a, and_1_out, and_9_out, b, c, change_sign, d, d_ff_11_q, d_ff_12_q, d_ff_13_q, d_ff_13_qn, e,
       en_2, f, g, h, i, M_D1, M_D2, not_1_out, not_2_out, not_3_out, not_4_out, not_5_out, not_6_out,
       or_3_out, or_4_out, or_5_out, or_8_out, or_9_out, or_10_out, or_11_out, or_12_out, or_13_out, pier_t,
       Pre_ans, rejestr_8_1_minus_a, row, SIGN, Stop, stop_p, stop_plus_minus, stop_t, stop_t_t, stop_t_t_t,
       stopx, sum_sub_neg_1_minus, transistor_29_out, transistor_43_out, tunnel, tunnel_t, tunnel_t_t,
       tunnel_t_t_t, tunnel_t_t_t_t_t, tunnel_t_t_t_t_t_t_t_t, xor_1_out, xx;
  wire [7:0] _1, _2, _5, _6, _7, _8, _9, _10, _11, bit_manipulation_1_val2, bit_manipulation_1_val_1, comp_1,
       div_8_1_out_4, multi_8_1_out_4, procent_1_val_out, rejestr_8_1_var_a, rejestr_8_1_var_b, sqrt_1_out_3,
       sum_sub_neg_1_val_out, transistor_14_out, transistor_25_out;

  Transistor #(.width(8)) transistor_1 (.in({8{1'b0}}), .out(_1), .gate(tunnel_t));
  not not_1 (not_1_out, SIGN);
  or or_1 (SIGN, CLEAR, in_5, in_6, x, in_8, in_13);
  or or_2 (row, in_11, pier, in_10, in_12);
  Transistor transistor_2 (.in(1'b0), .out(_3), .gate(tunnel_t));
  Transistor #(.gate("br"), .width(8)) transistor_3 (.in({8{1'b0}}), .out(_2), .gate(tunnel_t));
  not not_2 (not_2_out, not_3_out);
  not not_3 (not_3_out, not_4_out);
  not not_4 (not_4_out, not_1_out);
  not not_5 (not_5_out, not_2_out);
  Transistor #(.gate("br")) transistor_4 (.in(1'b0), .out(_4), .gate(tunnel_t));
  not not_6 (not_6_out, not_5_out);
  or or_3 (or_3_out, pier, not_6_out);
  or or_4 (or_4_out, in_11, in_12, not_6_out);
  or or_5 (or_5_out, in_12, in_11, not_6_out);
  Register #(.width(1)) register_1 (.D(row), .Q(i), .clk(row), .clr(Change));  // open: en
  or or_6 (Change, not_6_out, eneble);
  Transistor #(.width(8)) transistor_5 (.in({8{1'b0}}), .out(_5), .gate(xx));
  Transistor #(.gate("br"), .width(8)) transistor_6 (.in({8{1'b0}}), .out(_6), .gate(xx));
  D_Flip_Flop d_ff_1 (.clk(not_6_out), .D(in_5), .Q(a), .reset(stop_t));  // open: Qn, preset, en
  D_Flip_Flop d_ff_2 (.clk(not_6_out), .D(in_6), .Q(b), .reset(stop_t));  // open: Qn, preset, en
  D_Flip_Flop d_ff_3 (.clk(not_6_out), .D(x), .Q(c), .reset(stop_t));  // open: Qn, preset, en
  D_Flip_Flop d_ff_4 (.clk(not_6_out), .D(in_8), .Q(d), .reset(stop_t));  // open: Qn, preset, en
  D_Flip_Flop d_ff_5 (.clk(or_3_out), .D(pier), .Q(e));  // open: Qn, preset, en, reset
  D_Flip_Flop d_ff_6 (.clk(or_4_out), .D(in_11), .Q(f), .reset(stop_t));  // open: Qn, preset, en
  D_Flip_Flop d_ff_7 (.clk(or_5_out), .D(in_12), .Q(g), .reset(stop_t));  // open: Qn, preset, en
  D_Flip_Flop d_ff_8 (.clk(not_6_out), .D(in_13), .Q(h), .reset(stop_t));  // open: Qn, preset, en
  Transistor #(.width(8)) transistor_7 (.in({8{1'b0}}), .out(_7), .gate(tunnel_t_t_t));
  Transistor #(.gate("br"), .width(8)) transistor_8 (.in({8{1'b0}}), .out(_8), .gate(tunnel_t_t_t));
  Transistor #(.width(8)) transistor_9 (.in({8{1'b0}}), .out(_9), .gate(pier_t));
  REJESTR_8 rejestr_8_1 (
    .varA(VAL_IN), .var_A(rejestr_8_1_var_a), .clcA(change_sign), .Var_B(rejestr_8_1_var_b), .clcB(i),
    .reset(CLEAR), .enable(eneble), .enab(en_2), .varA_neg(in_2), .Minus_A(rejestr_8_1_minus_a),
    .Minus_B(M_D1));
  and and_1 (and_1_out, a, en_2, i);
  and and_2 (tunnel_t_t, b, en_2, i);
  and and_3 (xx, c, en_2, i);
  and and_4 (tunnel_t_t_t, d, en_2, i);
  and and_5 (pier_t, e, en_2, i);
  and and_6 (tunnel_t_t_t_t_t, f, en_2, i);
  and and_7 (tunnel_t_t_t_t_t_t_t_t, g, en_2, i);
  and and_8 (tunnel, h, en_2, i);
  Transistor #(.gate("br"), .width(8)) transistor_10 (.in({8{1'b0}}), .out(_11), .gate(tunnel));
  Transistor #(.width(8)) transistor_11 (.in({8{1'b0}}), .out(_10), .gate(tunnel));
  or or_7 (tunnel_t, and_1_out, tunnel_t_t);
  or or_8 (or_8_out, tunnel_t_t_t_t_t, tunnel_t_t_t_t_t_t_t_t);
  Transistor transistor_12 (.in(rejestr_8_1_minus_a), .out(M_D2), .gate(Pre_ans));
  Transistor #(.\type ("n")) transistor_13 (.in(d_ff_11_q), .out(M_D2), .gate(Pre_ans));
  Transistor #(.width(8)) transistor_14 (.in(rejestr_8_1_var_a), .out(transistor_14_out), .gate(Pre_ans));
  Transistor #(.\type ("n"), .width(8)) transistor_15 (.in(ans), .out(transistor_14_out), .gate(Pre_ans));
  Transistor #(.\type ("n")) transistor_16 (.in(M_D1), .out(_3), .gate(tunnel_t));
  Transistor #(.\type ("n"), .gate("br"), .width(8)) transistor_17 (.in(rejestr_8_1_var_b), .out(_1), .gate(tunnel_t));
  or or_9 (or_9_out, stopx, stop_plus_minus, stop_plus_minus, Stop, stop_t_t_t, stop_p, stop_t_t);
  Transistor #(.\type ("n")) transistor_18 (.in(M_D2), .out(_4), .gate(tunnel_t));
  Transistor #(.\type ("n"), .gate("br"), .width(8)) transistor_19 (.in(transistor_14_out), .out(_2), .gate(tunnel_t));
  Transistor #(.\type ("n"), .width(8)) transistor_20 (.in(rejestr_8_1_var_b), .out(_5), .gate(xx));
  Transistor #(.\type ("n"), .gate("br"), .width(8)) transistor_21 (.in(transistor_14_out), .out(_6), .gate(xx));
  Transistor #(.\type ("n"), .width(8)) transistor_22 (.in(transistor_14_out), .out(_7), .gate(tunnel_t_t_t));
  Transistor #(.\type ("n"), .gate("br"), .width(8)) transistor_23 (
    .in(rejestr_8_1_var_b), .out(_8), .gate(tunnel_t_t_t));
  SQRT sqrt_1 (.in_1(_9), .out_3(sqrt_1_out_3), .stop(stop_p), .in_2(pier_t));
  Transistor #(.\type ("n"), .gate("br"), .width(8)) transistor_24 (.in(rejestr_8_1_var_b), .out(_9), .gate(pier_t));
  Transistor #(.\type ("n"), .gate("br"), .width(8)) transistor_25 (
    .in(rejestr_8_1_var_b), .out(transistor_25_out), .gate(or_8_out));
  BIT_MANIPULATION bit_manipulation_1 (
    .val_in(transistor_25_out), .val_1(bit_manipulation_1_val_1), .val2(bit_manipulation_1_val2),
    .start(or_8_out), .stop(Stop));
  Transistor #(.\type ("n"), .width(8)) transistor_26 (.in(transistor_14_out), .out(_10), .gate(tunnel));
  Transistor #(.\type ("n"), .gate("br"), .width(8)) transistor_27 (.in(rejestr_8_1_var_b), .out(_11), .gate(tunnel));
  D_Flip_Flop d_ff_9 (.clk(or_9_out), .D(or_9_out), .Q(stop_t), .reset(or_10_out));  // open: Qn, preset, en
  or or_10 (or_10_out, eneble, SIGN);
  Transistor #(.\type ("n"), .width(8)) transistor_28 (.in(sum_sub_neg_1_val_out), .out(comp_1), .gate(tunnel_t));
  Sum_sub_neg sum_sub_neg_1 (
    .X__minus(_3), .Val_X(_1), .Y__minus(_4), .Val_Y(_2), .Start(tunnel_t), .val_out(sum_sub_neg_1_val_out),
    .minus(sum_sub_neg_1_minus), .in_1(tunnel_t_t), .stop(stop_plus_minus));
  Transistor #(.\type ("n"), .gate("br")) transistor_29 (
    .in(sum_sub_neg_1_minus), .out(transistor_29_out), .gate(tunnel_t));
  MULTI_8 multi_8_1 (.in_1(_5), .in_2(_6), .out_4(multi_8_1_out_4), .start(xx), .stop(stopx));  // open: out_5
  DIV_8 div_8_1 (.in_1(_7), .out_4(div_8_1_out_4), .in_3(_8), .start(tunnel_t_t_t), .stop(stop_t_t_t));
  PROCENT procent_1 (.Val(_10), .in_2(_11), .start(tunnel), .val_out(procent_1_val_out), .stop(stop_t_t));
  or or_11 (or_11_out, xx, tunnel_t_t_t_t_t_t_t_t, tunnel_t, tunnel_t, tunnel_t_t_t, pier_t, tunnel_t_t_t_t_t, tunnel);
  Transistor #(.gate("br"), .width(8)) transistor_30 (.in(VAL_IN), .out(Disp), .gate(i));
  REJESTR_8 rejestr_8_2 (.in_1(comp_1), .out_4(ans), .clc(stop_t), .reset(CLEAR));
  Transistor #(.\type ("n"), .width(8)) transistor_31 (.in(multi_8_1_out_4), .out(comp_1), .gate(xx));
  Transistor #(.\type ("n"), .width(8)) transistor_32 (.in(div_8_1_out_4), .out(comp_1), .gate(tunnel_t_t_t));
  Transistor #(.\type ("n"), .width(8)) transistor_33 (.in(sqrt_1_out_3), .out(comp_1), .gate(pier_t));
  or or_12 (or_12_out, xx, tunnel_t_t_t);
  Transistor #(.\type ("n")) transistor_34 (.in(xor_1_out), .out(transistor_29_out), .gate(or_12_out));
  Transistor #(.\type ("n"), .width(8)) transistor_35 (
    .in(bit_manipulation_1_val_1), .out(comp_1), .gate(tunnel_t_t_t_t_t_t_t_t));
  Transistor #(.\type ("n"), .gate("br"), .width(8)) transistor_36 (
    .in(bit_manipulation_1_val2), .out(comp_1), .gate(tunnel_t_t_t_t_t));
  Transistor #(.\type ("n"), .width(8)) transistor_37 (.in(procent_1_val_out), .out(comp_1), .gate(tunnel));
  Transistor #(.gate("br")) transistor_38 (.in(1'b0), .out(transistor_29_out), .gate(or_11_out));
  Transistor #(.width(8)) transistor_39 (.in({8{1'b0}}), .out(comp_1), .gate(or_11_out));
  D_Flip_Flop d_ff_10 (.clk(i), .D(i), .Q(comp), .reset(stop_t));  // open: Qn, preset, en
  Transistor #(.\type ("n"), .width(8)) transistor_40 (.in(ans), .out(Disp), .gate(i));
  Transistor #(.gate("br")) transistor_41 (.in(in_2), .out(disp_neg), .gate(i));
  D_Flip_Flop d_ff_11 (.clk(stop_t), .D(transistor_29_out), .Q(d_ff_11_q), .reset(CLEAR));  // open: Qn, preset, en
  xor xor_1 (xor_1_out, M_D1, M_D2);
  Transistor #(.\type ("n")) transistor_42 (.in(d_ff_11_q), .out(disp_neg), .gate(i));
  D_Flip_Flop d_ff_12 (.clk(row), .D(row), .Q(d_ff_12_q), .reset(transistor_43_out));  // open: Qn, preset, en
  Transistor #(.\type ("n"), .gate("br")) transistor_43 (.in(1'b0), .out(transistor_43_out), .gate(d_ff_13_q));
  Transistor transistor_44 (.in(eneble), .out(transistor_43_out), .gate(d_ff_13_q));
  D_Flip_Flop d_ff_13 (.clk(SIGN), .D(SIGN), .Q(d_ff_13_q), .Qn(d_ff_13_qn), .reset(row));  // open: preset, en
  and and_9 (and_9_out, d_ff_12_q, d_ff_13_qn);
  D_Flip_Flop d_ff_14 (.clk(stop_t), .D(and_9_out), .Q(Pre_ans), .reset(or_13_out));  // open: Qn, preset, en
  or or_13 (or_13_out, CLEAR, transistor_43_out);
  or or_14 (change_sign, d, c, b, a, e, g, f, h);

  // Other names for the same wires on the sheet: comp_2[7:0] = comp_1; en = eneble; neg_in = in_2; peir = pier;
  //   tunnel_t_t_t_t = in_11; tunnel_t_t_t_t_t_t = in_10; tunnel_t_t_t_t_t_t_t = in_12; value_in[7:0] = VAL_IN
endmodule
