// Logisim project MULTI_8v4.circ as structural Verilog: 1 circuit, main circuit MULTI_8
module MULTI_8 (
  input  [7:0] in_1,
  input  [7:0] in_2,
  input  start,
  output [7:0] out_4,
  output [15:0] out_5,
  output stop
);

  wire and_1_out, and_2_out, and_3_out, and_4_out, and_5_out, and_6_out, and_7_out, and_8_out, and_9_out,
       and_10_out, and_11_out, and_12_out, and_13_out, and_14_out, and_15_out, and_16_out, and_17_out,
       and_18_out, and_19_out, and_20_out, and_21_out, and_22_out, and_23_out, and_24_out, and_25_out,
       and_26_out, and_27_out, and_28_out, and_29_out, and_30_out, and_31_out, and_32_out, and_33_out,
       and_34_out, and_35_out, and_36_out, and_37_out, and_38_out, and_39_out, and_40_out, and_41_out,
       and_42_out, and_43_out, and_44_out, and_45_out, and_46_out, and_47_out, and_48_out, and_49_out,
       and_50_out, and_51_out, and_52_out, and_53_out, and_54_out, and_55_out, and_56_out, and_57_out,
       and_58_out, and_59_out, and_60_out, and_61_out, and_62_out, and_63_out, and_64_out, del_comp_8_1_out,
       hsum_1_carry, hsum_2_carry, hsum_3_carry, hsum_4_carry, hsum_5_carry, hsum_6_carry, hsum_7_carry,
       hsum_8_carry, not_1_out, not_2_out, not_4_out, sum_1_1_out_4, sum_1_1_out_5, sum_1_3_out_4,
       sum_1_3_out_5, sum_1_4_out_4, sum_1_4_out_5, sum_1_5_out_4, sum_1_5_out_5, sum_1_6_out_4,
       sum_1_6_out_5, sum_1_7_out_4, sum_1_7_out_5, sum_1_8_out_5, sum_1_9_out_5, sum_1_10_out_4,
       sum_1_10_out_5, sum_1_11_out_4, sum_1_11_out_5, sum_1_12_out_4, sum_1_12_out_5, sum_1_13_out_4,
       sum_1_13_out_5, sum_1_14_out_4, sum_1_14_out_5, sum_1_15_out_4, sum_1_15_out_5, sum_1_16_out_4,
       sum_1_16_out_5, sum_1_17_out_4, sum_1_17_out_5, sum_1_18_out_4, sum_1_18_out_5, sum_1_19_out_5,
       sum_1_20_out_5, sum_1_21_out_4, sum_1_21_out_5, sum_1_22_out_4, sum_1_22_out_5, sum_1_23_out_4,
       sum_1_23_out_5, sum_1_24_out_4, sum_1_24_out_5, sum_1_25_out_4, sum_1_25_out_5, sum_1_26_out_4,
       sum_1_26_out_5, sum_1_27_out_4, sum_1_27_out_5, sum_1_28_out_4, sum_1_28_out_5, sum_1_29_out_4,
       sum_1_29_out_5, sum_1_30_out_4, sum_1_30_out_5, sum_1_31_out_4, sum_1_31_out_5, sum_1_32_out_4,
       sum_1_32_out_5, sum_1_33_out_5, sum_1_34_out_4, sum_1_34_out_5, sum_1_35_out_4, sum_1_35_out_5,
       sum_1_36_out_4, sum_1_36_out_5, sum_1_37_out_4, sum_1_37_out_5, sum_1_38_out_4, sum_1_38_out_5,
       sum_1_39_out_4, sum_1_39_out_5, sum_1_40_out_4, sum_1_40_out_5, sum_1_41_out_4, sum_1_41_out_5,
       sum_1_42_out_4, sum_1_42_out_5, sum_1_43_out_4, sum_1_43_out_5, sum_1_44_out_4, sum_1_44_out_5,
       sum_1_45_out_5, sum_1_46_out_4, sum_1_46_out_5, sum_1_47_out_4, sum_1_47_out_5, sum_1_48_out_4,
       sum_1_48_out_5, sum_1_49_out_4, sum_1_49_out_5, sum_1_50_out_4, sum_1_50_out_5, sum_1_51_out_4,
       sum_1_51_out_5, sum_1_52_out_4, sum_1_52_out_5, sum_1_53_out_4, sum_1_53_out_5, sum_1_54_out_4,
       sum_1_54_out_5, sum_1_55_out_4, sum_1_55_out_5, sum_1_56_out_4, sum_1_56_out_5, transistor_1_out;

  and and_1 (and_1_out, in_1[7], in_2[6]);
  SUM_1 sum_1_1 (
    .in_1(and_1_out), .in_2(sum_1_5_out_5), .in_3(sum_1_7_out_5), .out_4(sum_1_1_out_4), .out_5(sum_1_1_out_5));
  and and_2 (and_2_out, in_1[7], in_2[7]);
  SUM_1 sum_1_2 (.in_1(and_2_out), .in_2(sum_1_1_out_5), .in_3(sum_1_8_out_5), .out_4(out_5[14]), .out_5(out_5[15]));
  and and_3 (and_3_out, in_1[7], in_2[3]);
  SUM_1 sum_1_3 (
    .in_1(and_3_out), .in_2(sum_1_11_out_5), .in_3(sum_1_13_out_5), .out_4(sum_1_3_out_4),
    .out_5(sum_1_3_out_5));
  and and_4 (and_4_out, in_1[7], in_2[4]);
  SUM_1 sum_1_4 (
    .in_1(and_4_out), .in_2(sum_1_3_out_5), .in_3(sum_1_14_out_5), .out_4(sum_1_4_out_4),
    .out_5(sum_1_4_out_5));
  and and_5 (and_5_out, in_1[7], in_2[5]);
  and and_6 (and_6_out, in_1[6], in_2[5]);
  SUM_1 sum_1_5 (
    .in_1(and_5_out), .in_2(sum_1_4_out_5), .in_3(sum_1_6_out_5), .out_4(sum_1_5_out_4), .out_5(sum_1_5_out_5));
  SUM_1 sum_1_6 (
    .in_1(and_6_out), .in_2(sum_1_4_out_4), .in_3(sum_1_16_out_5), .out_4(sum_1_6_out_4),
    .out_5(sum_1_6_out_5));
  and and_7 (and_7_out, in_1[6], in_2[6]);
  SUM_1 sum_1_7 (
    .in_1(and_7_out), .in_2(sum_1_5_out_4), .in_3(sum_1_18_out_5), .out_4(sum_1_7_out_4),
    .out_5(sum_1_7_out_5));
  and and_8 (and_8_out, in_1[5], in_2[7]);
  and and_9 (and_9_out, in_1[6], in_2[7]);
  SUM_1 sum_1_8 (
    .in_1(and_9_out), .in_2(sum_1_1_out_4), .in_3(sum_1_9_out_5), .out_4(out_5[13]), .out_5(sum_1_8_out_5));
  SUM_1 sum_1_9 (
    .in_1(and_8_out), .in_2(sum_1_7_out_4), .in_3(sum_1_19_out_5), .out_4(out_5[12]), .out_5(sum_1_9_out_5));
  and and_10 (and_10_out, in_1[7], in_2[1]);
  SUM_1 sum_1_10 (
    .in_1(and_10_out), .in_2(sum_1_22_out_5), .in_3(sum_1_24_out_5), .out_4(sum_1_10_out_4),
    .out_5(sum_1_10_out_5));
  and and_11 (and_11_out, in_1[6], in_2[2]);
  and and_12 (and_12_out, in_1[7], in_2[2]);
  SUM_1 sum_1_11 (
    .in_1(and_12_out), .in_2(sum_1_10_out_5), .in_3(sum_1_12_out_5), .out_4(sum_1_11_out_4),
    .out_5(sum_1_11_out_5));
  SUM_1 sum_1_12 (
    .in_1(and_11_out), .in_2(sum_1_10_out_4), .in_3(sum_1_25_out_5), .out_4(sum_1_12_out_4),
    .out_5(sum_1_12_out_5));
  and and_13 (and_13_out, in_1[6], in_2[3]);
  SUM_1 sum_1_13 (
    .in_1(and_13_out), .in_2(sum_1_11_out_4), .in_3(sum_1_26_out_5), .out_4(sum_1_13_out_4),
    .out_5(sum_1_13_out_5));
  and and_14 (and_14_out, in_1[6], in_2[4]);
  and and_15 (and_15_out, in_1[5], in_2[4]);
  SUM_1 sum_1_14 (
    .in_1(and_14_out), .in_2(sum_1_3_out_4), .in_3(sum_1_15_out_5), .out_4(sum_1_14_out_4),
    .out_5(sum_1_14_out_5));
  SUM_1 sum_1_15 (
    .in_1(and_15_out), .in_2(sum_1_13_out_4), .in_3(sum_1_28_out_5), .out_4(sum_1_15_out_4),
    .out_5(sum_1_15_out_5));
  and and_16 (and_16_out, in_1[5], in_2[5]);
  SUM_1 sum_1_16 (
    .in_1(and_16_out), .in_2(sum_1_14_out_4), .in_3(sum_1_30_out_5), .out_4(sum_1_16_out_4),
    .out_5(sum_1_16_out_5));
  and and_17 (and_17_out, in_1[5], in_2[6]);
  and and_18 (and_18_out, in_1[4], in_2[6]);
  SUM_1 sum_1_17 (
    .in_1(and_18_out), .in_2(sum_1_16_out_4), .in_3(sum_1_32_out_5), .out_4(sum_1_17_out_4),
    .out_5(sum_1_17_out_5));
  SUM_1 sum_1_18 (
    .in_1(and_17_out), .in_2(sum_1_6_out_4), .in_3(sum_1_17_out_5), .out_4(sum_1_18_out_4),
    .out_5(sum_1_18_out_5));
  and and_19 (and_19_out, in_1[3], in_2[7]);
  and and_20 (and_20_out, in_1[4], in_2[7]);
  SUM_1 sum_1_19 (
    .in_1(and_20_out), .in_2(sum_1_18_out_4), .in_3(sum_1_20_out_5), .out_4(out_5[11]), .out_5(sum_1_19_out_5));
  SUM_1 sum_1_20 (
    .in_1(and_19_out), .in_2(sum_1_17_out_4), .in_3(sum_1_33_out_5), .out_4(out_5[10]), .out_5(sum_1_20_out_5));
  and and_21 (and_21_out, in_1[6], in_2[0]);
  and and_22 (and_22_out, in_1[7], in_2[0]);
  SUM_1 sum_1_21 (
    .in_1(and_21_out), .in_2(1'b0), .in_3(sum_1_34_out_5), .out_4(sum_1_21_out_4), .out_5(sum_1_21_out_5));
  SUM_1 sum_1_22 (
    .in_1(and_22_out), .in_2(1'b0), .in_3(sum_1_21_out_5), .out_4(sum_1_22_out_4), .out_5(sum_1_22_out_5));
  and and_23 (and_23_out, in_1[5], in_2[1]);
  and and_24 (and_24_out, in_1[6], in_2[1]);
  SUM_1 sum_1_23 (
    .in_1(and_23_out), .in_2(sum_1_21_out_4), .in_3(sum_1_36_out_5), .out_4(sum_1_23_out_4),
    .out_5(sum_1_23_out_5));
  SUM_1 sum_1_24 (
    .in_1(and_24_out), .in_2(sum_1_22_out_4), .in_3(sum_1_23_out_5), .out_4(sum_1_24_out_4),
    .out_5(sum_1_24_out_5));
  and and_25 (and_25_out, in_1[5], in_2[2]);
  SUM_1 sum_1_25 (
    .in_1(and_25_out), .in_2(sum_1_24_out_4), .in_3(sum_1_38_out_5), .out_4(sum_1_25_out_4),
    .out_5(sum_1_25_out_5));
  and and_26 (and_26_out, in_1[4], in_2[3]);
  and and_27 (and_27_out, in_1[5], in_2[3]);
  SUM_1 sum_1_26 (
    .in_1(and_27_out), .in_2(sum_1_12_out_4), .in_3(sum_1_27_out_5), .out_4(sum_1_26_out_4),
    .out_5(sum_1_26_out_5));
  SUM_1 sum_1_27 (
    .in_1(and_26_out), .in_2(sum_1_25_out_4), .in_3(sum_1_39_out_5), .out_4(sum_1_27_out_4),
    .out_5(sum_1_27_out_5));
  and and_28 (and_28_out, in_1[4], in_2[4]);
  SUM_1 sum_1_28 (
    .in_1(and_28_out), .in_2(sum_1_26_out_4), .in_3(sum_1_40_out_5), .out_4(sum_1_28_out_4),
    .out_5(sum_1_28_out_5));
  and and_29 (and_29_out, in_1[3], in_2[5]);
  and and_30 (and_30_out, in_1[4], in_2[5]);
  SUM_1 sum_1_29 (
    .in_1(and_29_out), .in_2(sum_1_28_out_4), .in_3(sum_1_43_out_5), .out_4(sum_1_29_out_4),
    .out_5(sum_1_29_out_5));
  SUM_1 sum_1_30 (
    .in_1(and_30_out), .in_2(sum_1_15_out_4), .in_3(sum_1_29_out_5), .out_4(sum_1_30_out_4),
    .out_5(sum_1_30_out_5));
  and and_31 (and_31_out, in_1[3], in_2[6]);
  and and_32 (and_32_out, in_1[2], in_2[6]);
  SUM_1 sum_1_31 (
    .in_1(and_32_out), .in_2(sum_1_29_out_4), .in_3(sum_1_44_out_5), .out_4(sum_1_31_out_4),
    .out_5(sum_1_31_out_5));
  SUM_1 sum_1_32 (
    .in_1(and_31_out), .in_2(sum_1_30_out_4), .in_3(sum_1_31_out_5), .out_4(sum_1_32_out_4),
    .out_5(sum_1_32_out_5));
  and and_33 (and_33_out, in_1[2], in_2[7]);
  SUM_1 sum_1_33 (
    .in_1(and_33_out), .in_2(sum_1_32_out_4), .in_3(sum_1_45_out_5), .out_4(out_5[9]), .out_5(sum_1_33_out_5));
  and and_34 (and_34_out, in_1[5], in_2[0]);
  and and_35 (and_35_out, in_1[4], in_2[0]);
  SUM_1 sum_1_34 (
    .in_1(and_34_out), .in_2(1'b0), .in_3(sum_1_35_out_5), .out_4(sum_1_34_out_4), .out_5(sum_1_34_out_5));
  SUM_1 sum_1_35 (
    .in_1(and_35_out), .in_2(1'b0), .in_3(sum_1_46_out_5), .out_4(sum_1_35_out_4), .out_5(sum_1_35_out_5));
  and and_36 (and_36_out, in_1[4], in_2[1]);
  SUM_1 sum_1_36 (
    .in_1(and_36_out), .in_2(sum_1_34_out_4), .in_3(sum_1_48_out_5), .out_4(sum_1_36_out_4),
    .out_5(sum_1_36_out_5));
  and and_37 (and_37_out, in_1[4], in_2[2]);
  and and_38 (and_38_out, in_1[3], in_2[2]);
  SUM_1 sum_1_37 (
    .in_1(and_38_out), .in_2(sum_1_36_out_4), .in_3(sum_1_49_out_5), .out_4(sum_1_37_out_4),
    .out_5(sum_1_37_out_5));
  SUM_1 sum_1_38 (
    .in_1(and_37_out), .in_2(sum_1_23_out_4), .in_3(sum_1_37_out_5), .out_4(sum_1_38_out_4),
    .out_5(sum_1_38_out_5));
  and and_39 (and_39_out, in_1[3], in_2[3]);
  SUM_1 sum_1_39 (
    .in_1(and_39_out), .in_2(sum_1_38_out_4), .in_3(sum_1_50_out_5), .out_4(sum_1_39_out_4),
    .out_5(sum_1_39_out_5));
  and and_40 (and_40_out, in_1[2], in_2[4]);
  and and_41 (and_41_out, in_1[3], in_2[4]);
  SUM_1 sum_1_40 (
    .in_1(and_41_out), .in_2(sum_1_27_out_4), .in_3(sum_1_41_out_5), .out_4(sum_1_40_out_4),
    .out_5(sum_1_40_out_5));
  SUM_1 sum_1_41 (
    .in_1(and_40_out), .in_2(sum_1_39_out_4), .in_3(sum_1_52_out_5), .out_4(sum_1_41_out_4),
    .out_5(sum_1_41_out_5));
  and and_42 (and_42_out, in_1[2], in_2[5]);
  and and_43 (and_43_out, in_1[1], in_2[5]);
  SUM_1 sum_1_42 (
    .in_1(and_43_out), .in_2(sum_1_41_out_4), .in_3(hsum_2_carry), .out_4(sum_1_42_out_4),
    .out_5(sum_1_42_out_5));
  SUM_1 sum_1_43 (
    .in_1(and_42_out), .in_2(sum_1_40_out_4), .in_3(sum_1_42_out_5), .out_4(sum_1_43_out_4),
    .out_5(sum_1_43_out_5));
  and and_44 (and_44_out, in_1[1], in_2[6]);
  SUM_1 sum_1_44 (
    .in_1(and_44_out), .in_2(sum_1_43_out_4), .in_3(hsum_3_carry), .out_4(sum_1_44_out_4),
    .out_5(sum_1_44_out_5));
  and and_45 (and_45_out, in_1[1], in_2[7]);
  and and_46 (and_46_out, in_1[0], in_2[7]);
  HSUM hsum_1 (.X(and_46_out), .Y(sum_1_44_out_4), .Sum(out_4[7]), .Carry(hsum_1_carry));
  SUM_1 sum_1_45 (
    .in_1(and_45_out), .in_2(sum_1_31_out_4), .in_3(hsum_1_carry), .out_4(out_5[8]), .out_5(sum_1_45_out_5));
  and and_47 (and_47_out, in_1[3], in_2[0]);
  SUM_1 sum_1_46 (
    .in_1(and_47_out), .in_2(1'b0), .in_3(sum_1_53_out_5), .out_4(sum_1_46_out_4), .out_5(sum_1_46_out_5));
  and and_48 (and_48_out, in_1[2], in_2[1]);
  and and_49 (and_49_out, in_1[3], in_2[1]);
  SUM_1 sum_1_47 (
    .in_1(and_48_out), .in_2(sum_1_46_out_4), .in_3(sum_1_55_out_5), .out_4(sum_1_47_out_4),
    .out_5(sum_1_47_out_5));
  SUM_1 sum_1_48 (
    .in_1(and_49_out), .in_2(sum_1_35_out_4), .in_3(sum_1_47_out_5), .out_4(sum_1_48_out_4),
    .out_5(sum_1_48_out_5));
  and and_50 (and_50_out, in_1[2], in_2[2]);
  SUM_1 sum_1_49 (
    .in_1(and_50_out), .in_2(sum_1_48_out_4), .in_3(sum_1_56_out_5), .out_4(sum_1_49_out_4),
    .out_5(sum_1_49_out_5));
  and and_51 (and_51_out, in_1[2], in_2[3]);
  and and_52 (and_52_out, in_1[1], in_2[3]);
  SUM_1 sum_1_50 (
    .in_1(and_51_out), .in_2(sum_1_37_out_4), .in_3(sum_1_51_out_5), .out_4(sum_1_50_out_4),
    .out_5(sum_1_50_out_5));
  SUM_1 sum_1_51 (
    .in_1(and_52_out), .in_2(sum_1_49_out_4), .in_3(hsum_5_carry), .out_4(sum_1_51_out_4),
    .out_5(sum_1_51_out_5));
  and and_53 (and_53_out, in_1[1], in_2[4]);
  SUM_1 sum_1_52 (
    .in_1(and_53_out), .in_2(sum_1_50_out_4), .in_3(hsum_6_carry), .out_4(sum_1_52_out_4),
    .out_5(sum_1_52_out_5));
  and and_54 (and_54_out, in_1[0], in_2[5]);
  HSUM hsum_2 (.X(and_54_out), .Y(sum_1_52_out_4), .Sum(out_4[5]), .Carry(hsum_2_carry));
  and and_55 (and_55_out, in_1[0], in_2[6]);
  HSUM hsum_3 (.X(and_55_out), .Y(sum_1_42_out_4), .Sum(out_4[6]), .Carry(hsum_3_carry));
  and and_56 (and_56_out, in_1[1], in_2[0]);
  and and_57 (and_57_out, in_1[2], in_2[0]);
  SUM_1 sum_1_53 (
    .in_1(and_57_out), .in_2(1'b0), .in_3(sum_1_54_out_5), .out_4(sum_1_53_out_4), .out_5(sum_1_53_out_5));
  SUM_1 sum_1_54 (.in_1(and_56_out), .in_2(1'b0), .in_3(hsum_7_carry), .out_4(sum_1_54_out_4), .out_5(sum_1_54_out_5));
  and and_58 (and_58_out, in_1[1], in_2[1]);
  SUM_1 sum_1_55 (
    .in_1(and_58_out), .in_2(sum_1_53_out_4), .in_3(hsum_8_carry), .out_4(sum_1_55_out_4),
    .out_5(sum_1_55_out_5));
  and and_59 (and_59_out, in_1[1], in_2[2]);
  and and_60 (and_60_out, in_1[0], in_2[2]);
  HSUM hsum_4 (.X(and_60_out), .Y(sum_1_55_out_4), .Sum(out_4[2]), .Carry(hsum_4_carry));
  SUM_1 sum_1_56 (
    .in_1(and_59_out), .in_2(sum_1_47_out_4), .in_3(hsum_4_carry), .out_4(sum_1_56_out_4),
    .out_5(sum_1_56_out_5));
  and and_61 (and_61_out, in_1[0], in_2[3]);
  HSUM hsum_5 (.X(and_61_out), .Y(sum_1_56_out_4), .Sum(out_4[3]), .Carry(hsum_5_carry));
  and and_62 (and_62_out, in_1[0], in_2[4]);
  HSUM hsum_6 (.X(and_62_out), .Y(sum_1_51_out_4), .Sum(out_4[4]), .Carry(hsum_6_carry));
  and and_63 (and_63_out, in_1[0], in_2[0]);
  HSUM hsum_7 (.X(and_63_out), .Y(1'b0), .Sum(out_4[0]), .Carry(hsum_7_carry));
  and and_64 (and_64_out, in_1[0], in_2[1]);
  HSUM hsum_8 (.X(and_64_out), .Y(sum_1_54_out_4), .Sum(out_4[1]), .Carry(hsum_8_carry));
  Del_comp_8 del_comp_8_1 (.var_2_in(out_4), .start(start), .out(del_comp_8_1_out));  // open: var_2_out
  Transistor transistor_1 (.in(1'b0), .out(transistor_1_out), .gate(del_comp_8_1_out));
  Transistor #(.\type ("n")) transistor_2 (.in(start), .out(transistor_1_out), .gate(del_comp_8_1_out));
  not not_1 (not_1_out, not_2_out);
  not not_2 (not_2_out, transistor_1_out);
  not not_3 (stop, not_4_out);
  not not_4 (not_4_out, not_1_out);

  assign out_5[7:0] = out_4;
endmodule
