// Logisim project PROCENT.circ as structural Verilog: 1 circuit, main circuit PROCENT
module PROCENT (
  input  [7:0] Val,
  input  [7:0] in_2,
  input  start,
  output [7:0] val_out,
  output stop
);

  wire multi_8_1_stop;
  wire [15:0] multi_8_1_out_5;

  MULTI_8 multi_8_1 (
    .in_1(Val), .in_2(in_2), .out_5(multi_8_1_out_5), .start(start), .stop(multi_8_1_stop));  // open: out_4
  DIV_16 div_16_1 (.in_1(multi_8_1_out_5), .in_2(multi_8_1_stop), .out_4(val_out), .out_5(stop), .in_3(16'h64));
endmodule
