// Logisim project PU.circ as structural Verilog: 1 circuit, main circuit PU
module PU (
  input  dzielnik,
  input  reszta,
  input  \równa ,
  input  var_out,
  output \równa_out ,
  output reszta_out
);

  wire and_1_out, and_2_out, not_1_out, not_2_out, sum_1_1_out_4;

  not not_1 (not_1_out, var_out);
  not not_2 (not_2_out, dzielnik);
  SUM_1 sum_1_1 (.in_1(not_2_out), .in_2(reszta), .in_3(\równa ), .out_4(sum_1_1_out_4), .out_5(\równa_out ));
  and and_1 (and_1_out, var_out, sum_1_1_out_4);
  and and_2 (and_2_out, not_1_out, reszta);
  or or_1 (reszta_out, and_1_out, and_2_out);
endmodule
