// Logisim project REJESTR_4.circ as structural Verilog: 1 circuit, main circuit REJESTR_4
module REJESTR_4 (
  input  [3:0] in_1,
  input  clc,
  input  reset,
  output [3:0] out_4
);

  D_Flip_Flop d_ff_1 (.clk(clc), .D(in_1[0]), .Q(out_4[0]), .reset(reset));  // open: Qn, preset, en
  D_Flip_Flop d_ff_2 (.clk(clc), .D(in_1[1]), .Q(out_4[1]), .reset(reset));  // open: Qn, preset, en
  D_Flip_Flop d_ff_3 (.clk(clc), .D(in_1[2]), .Q(out_4[2]), .reset(reset));  // open: Qn, preset, en
  D_Flip_Flop d_ff_4 (.clk(clc), .D(in_1[3]), .Q(out_4[3]), .reset(reset));  // open: Qn, preset, en
endmodule
