// Logisim project REJESTR_8.circ as structural Verilog: 1 circuit, main circuit REJESTR_8
module REJESTR_8 (
  input  [7:0] in_1,
  input  clc,
  input  reset,
  output [7:0] out_4
);

  D_Flip_Flop d_ff_1 (.clk(clc), .D(in_1[0]), .Q(out_4[0]), .reset(reset));  // open: Qn, preset, en
  D_Flip_Flop d_ff_2 (.clk(clc), .D(in_1[1]), .Q(out_4[1]), .reset(reset));  // open: Qn, preset, en
  D_Flip_Flop d_ff_3 (.clk(clc), .D(in_1[2]), .Q(out_4[2]), .reset(reset));  // open: Qn, preset, en
  D_Flip_Flop d_ff_4 (.clk(clc), .D(in_1[3]), .Q(out_4[3]), .reset(reset));  // open: Qn, preset, en
  D_Flip_Flop d_ff_5 (.clk(clc), .D(in_1[4]), .Q(out_4[4]), .reset(reset));  // open: Qn, preset, en
  D_Flip_Flop d_ff_6 (.clk(clc), .D(in_1[5]), .Q(out_4[5]), .reset(reset));  // open: Qn, preset, en
  D_Flip_Flop d_ff_7 (.clk(clc), .D(in_1[6]), .Q(out_4[6]), .reset(reset));  // open: Qn, preset, en
  D_Flip_Flop d_ff_8 (.clk(clc), .D(in_1[7]), .Q(out_4[7]), .reset(reset));  // open: Qn, preset, en
endmodule
