// Logisim project REJESTR_8_logic.circ as structural Verilog: 1 circuit, main circuit REJESTR_8
module REJESTR_8 (
  input  [7:0] varA,
  input  varA_neg,
  input  clcA,
  input  clcB,
  input  reset,
  input  enable,
  output Minus_A,
  output [7:0] var_A,
  output Minus_B,
  output [7:0] Var_B,
  output enab
);

  wire and_1_out, RE, transistor_1_out, transistor_2_out, transistor_5_out, transistor_6_out;

  D_Flip_Flop d_ff_1 (.clk(clcA), .D(varA[0]), .Q(var_A[0]), .reset(RE));  // open: Qn, preset, en
  D_Flip_Flop d_ff_2 (.clk(clcB), .D(varA[0]), .Q(Var_B[0]), .reset(RE));  // open: Qn, preset, en
  D_Flip_Flop d_ff_3 (.clk(clcA), .D(varA[1]), .Q(var_A[1]), .reset(RE));  // open: Qn, preset, en
  D_Flip_Flop d_ff_4 (.clk(clcB), .D(varA[1]), .Q(Var_B[1]), .reset(RE));  // open: Qn, preset, en
  Transistor #(.\type ("n")) transistor_1 (.in(transistor_2_out), .out(transistor_1_out), .gate(transistor_2_out));
  Transistor #(.\type ("n")) transistor_2 (.in(clcB), .out(transistor_2_out), .gate(clcB));
  Transistor transistor_3 (.in(1'b0), .out(transistor_1_out), .gate(transistor_2_out));
  Transistor transistor_4 (.in(1'b0), .out(transistor_2_out), .gate(clcB));
  D_Flip_Flop d_ff_5 (.clk(clcA), .D(varA[2]), .Q(var_A[2]), .reset(RE));  // open: Qn, preset, en
  D_Flip_Flop d_ff_6 (.clk(clcB), .D(varA[2]), .Q(Var_B[2]), .reset(RE));  // open: Qn, preset, en
  Transistor #(.\type ("n")) transistor_5 (.in(transistor_6_out), .out(transistor_5_out), .gate(transistor_6_out));
  Transistor #(.\type ("n")) transistor_6 (.in(transistor_1_out), .out(transistor_6_out), .gate(transistor_1_out));
  Transistor transistor_7 (.in(1'b0), .out(transistor_5_out), .gate(transistor_6_out));
  Transistor transistor_8 (.in(1'b0), .out(transistor_6_out), .gate(transistor_1_out));
  D_Flip_Flop d_ff_7 (.clk(clcA), .D(varA[3]), .Q(var_A[3]), .reset(RE));  // open: Qn, preset, en
  D_Flip_Flop d_ff_8 (.clk(clcB), .D(varA[3]), .Q(Var_B[3]), .reset(RE));  // open: Qn, preset, en
  Transistor #(.\type ("n")) transistor_9 (.in(transistor_5_out), .out(enab), .gate(transistor_5_out));
  Transistor transistor_10 (.in(1'b0), .out(enab), .gate(transistor_5_out));
  D_Flip_Flop d_ff_9 (.clk(clcA), .D(varA[4]), .Q(var_A[4]), .reset(RE));  // open: Qn, preset, en
  D_Flip_Flop d_ff_10 (.clk(clcB), .D(varA[4]), .Q(Var_B[4]), .reset(RE));  // open: Qn, preset, en
  D_Flip_Flop d_ff_11 (.clk(clcA), .D(varA[5]), .Q(var_A[5]), .reset(RE));  // open: Qn, preset, en
  D_Flip_Flop d_ff_12 (.clk(clcB), .D(varA[5]), .Q(Var_B[5]), .reset(RE));  // open: Qn, preset, en
  D_Flip_Flop d_ff_13 (.clk(clcA), .D(varA[6]), .Q(var_A[6]), .reset(RE));  // open: Qn, preset, en
  D_Flip_Flop d_ff_14 (.clk(clcB), .D(varA[6]), .Q(Var_B[6]), .reset(RE));  // open: Qn, preset, en
  D_Flip_Flop d_ff_15 (.clk(clcA), .D(varA[7]), .Q(var_A[7]), .reset(RE));  // open: Qn, preset, en
  D_Flip_Flop d_ff_16 (.clk(clcB), .D(varA[7]), .Q(Var_B[7]), .reset(RE));  // open: Qn, preset, en
  D_Flip_Flop d_ff_17 (.clk(clcA), .D(varA_neg), .Q(Minus_A), .reset(RE));  // open: Qn, preset, en
  D_Flip_Flop d_ff_18 (.clk(clcB), .D(varA_neg), .Q(Minus_B), .reset(RE));  // open: Qn, preset, en
  or or_1 (RE, reset, and_1_out);
  and and_1 (and_1_out, clcB, clcA, enable);
endmodule
