// Logisim project SQRT_8_v2.circ as structural Verilog: 1 circuit, main circuit SQRT
module SQRT (
  input  [7:0] in_1,
  input  in_2,
  output [7:0] out_3,
  output stop
);

  wire and_1_out, and_2_out, compare_8_1_a_2, compare_8_1_b_2, compare_8_2_a_2, compare_8_2_b_2,
       del_comp_8_1_out, del_comp_8_2_out, del_comp_8_3_out, del_comp_8_4_out, del_comp_8_5_out,
       del_comp_8_6_out, del_comp_8_7_out, not_1_out, not_2_out, not_3_out, sqrt_req_1_stop, sqrt_req_2_stop,
       sqrt_req_3_stop, transistor_6_out;
  wire [7:0] del_comp_8_1_var_2_out, del_comp_8_2_var_2_out, del_comp_8_3_var_2_out, del_comp_8_4_var_2_out,
       del_comp_8_5_var_2_out, del_comp_8_6_var_2_out, sqrt_req_1_out_4, sqrt_req_2_out_4, transistor_1_out,
       transistor_3_out;

  Del_comp_8 del_comp_8_1 (.var_2_in(in_1), .start(in_2), .var_2_out(del_comp_8_1_var_2_out), .out(del_comp_8_1_out));
  Del_comp_8 del_comp_8_2 (
    .var_2_in(del_comp_8_1_var_2_out), .start(del_comp_8_1_out), .var_2_out(del_comp_8_2_var_2_out),
    .out(del_comp_8_2_out));
  COMPARE_8 compare_8_1 (
    .A(8'ha), .B(del_comp_8_2_var_2_out), .A_2(compare_8_1_a_2), .B_2(compare_8_1_b_2));  // open: out_4
  and and_1 (and_1_out, compare_8_1_a_2, compare_8_2_a_2);
  Transistor #(.\type ("n"), .width(8)) transistor_1 (.in(8'h2), .out(transistor_1_out), .gate(and_1_out));
  COMPARE_8 compare_8_2 (
    .A(8'h64), .B(del_comp_8_2_var_2_out), .A_2(compare_8_2_a_2), .B_2(compare_8_2_b_2));  // open: out_4
  and and_2 (and_2_out, compare_8_1_b_2, compare_8_2_a_2);
  Transistor #(.\type ("n"), .width(8)) transistor_2 (.in(8'h6), .out(transistor_1_out), .gate(and_2_out));
  Transistor #(.width(8)) transistor_3 (.in({8{1'b0}}), .out(transistor_3_out), .gate(del_comp_8_2_out));
  Transistor #(.\type ("n"), .width(8)) transistor_4 (
    .in(transistor_1_out), .out(transistor_3_out), .gate(del_comp_8_2_out));
  SQRT_REQ sqrt_req_1 (
    .x0(transistor_3_out), .start(del_comp_8_2_out), .s(del_comp_8_2_var_2_out), .out_4(sqrt_req_1_out_4),
    .stop(sqrt_req_1_stop));
  Transistor #(.\type ("n"), .width(8)) transistor_5 (.in(8'h14), .out(transistor_1_out), .gate(compare_8_2_b_2));
  SQRT_REQ sqrt_req_2 (
    .x0(sqrt_req_1_out_4), .start(sqrt_req_1_stop), .s(del_comp_8_2_var_2_out), .out_4(sqrt_req_2_out_4),
    .stop(sqrt_req_2_stop));
  SQRT_REQ sqrt_req_3 (
    .x0(sqrt_req_2_out_4), .start(sqrt_req_2_stop), .s(del_comp_8_2_var_2_out), .out_4(out_3),
    .stop(sqrt_req_3_stop));
  Counter counter_1 (.clk(del_comp_8_7_out));  // open: load, D, count, Q, carry, clr
  Del_comp_8 del_comp_8_3 (
    .var_2_in(out_3), .start(sqrt_req_3_stop), .var_2_out(del_comp_8_3_var_2_out), .out(del_comp_8_3_out));
  Del_comp_8 del_comp_8_4 (
    .var_2_in(del_comp_8_3_var_2_out), .start(del_comp_8_3_out), .var_2_out(del_comp_8_4_var_2_out),
    .out(del_comp_8_4_out), .in_1(out_3));
  Del_comp_8 del_comp_8_5 (
    .var_2_in(del_comp_8_4_var_2_out), .start(del_comp_8_4_out), .var_2_out(del_comp_8_5_var_2_out),
    .out(del_comp_8_5_out), .in_1(out_3));
  Del_comp_8 del_comp_8_6 (
    .var_2_in(del_comp_8_5_var_2_out), .start(del_comp_8_5_out), .var_2_out(del_comp_8_6_var_2_out),
    .out(del_comp_8_6_out), .in_1(out_3));
  Del_comp_8 del_comp_8_7 (
    .var_2_in(del_comp_8_6_var_2_out), .start(del_comp_8_6_out), .out(del_comp_8_7_out), .in_1(out_3));  // open: var_2_out
  Transistor transistor_6 (.in(1'b0), .out(transistor_6_out), .gate(del_comp_8_7_out));
  Transistor #(.\type ("n")) transistor_7 (.in(del_comp_8_2_out), .out(transistor_6_out), .gate(del_comp_8_7_out));
  not not_1 (not_1_out, transistor_6_out);
  not not_2 (not_2_out, not_1_out);
  not not_3 (not_3_out, not_2_out);
  not not_4 (stop, not_3_out);
endmodule
