// Logisim project SQRT_REQv2.circ as structural Verilog: 1 circuit, main circuit SQRT_REQ
module SQRT_REQ (
  input  [7:0] s,
  input  [7:0] x0,
  input  start,
  output [7:0] out_4,
  output stop
);

  wire div_8_1_stop, sum_8_1_stop;
  wire [7:0] div_8_1_out_4, sum_8_1_out_4;

  DIV_8 div_8_1 (.in_1(s), .out_4(div_8_1_out_4), .in_3(x0), .start(start), .stop(div_8_1_stop));
  SUM_8 sum_8_1 (
    .in_1(div_8_1_out_4), .in_2(x0), .out_4(sum_8_1_out_4), .start(div_8_1_stop), .stop(sum_8_1_stop));  // open: out_5
  DIV_8 div_8_2 (.in_1(sum_8_1_out_4), .out_4(out_4), .in_3(8'h2), .start(sum_8_1_stop), .stop(stop));
endmodule
