// Logisim project SUB_SEQUENCEv2.circ as structural Verilog: 1 circuit, main circuit SUB_SEQUENCE
module SUB_SEQUENCE (
  input  [7:0] in_1,
  input  [7:0] in_2,
  input  start,
  output [7:0] out_4,
  output [7:0] out_5,
  output Stop
);

  wire compare_8_1_a_2, compare_8_1_b_2, compare_8_1_out_4, or_1_out;
  wire [7:0] del_comp_8_1_var_2_out, transistor_1_out, transistor_2_out;

  Del_comp_8 del_comp_8_1 (.var_2_in(in_2), .start(start), .var_2_out(del_comp_8_1_var_2_out), .out(Stop));
  or or_1 (or_1_out, compare_8_1_a_2, compare_8_1_out_4);
  COMPARE_8 compare_8_1 (
    .A(del_comp_8_1_var_2_out), .B(in_1), .A_2(compare_8_1_a_2), .out_4(compare_8_1_out_4),
    .B_2(compare_8_1_b_2));
  Transistor #(.width(8)) transistor_1 (.in(in_1), .out(transistor_1_out), .gate(or_1_out));
  Transistor #(.width(8)) transistor_2 (.in(del_comp_8_1_var_2_out), .out(transistor_2_out), .gate(or_1_out));
  Transistor #(.width(8)) transistor_3 (.in(in_1), .out(transistor_2_out), .gate(compare_8_1_b_2));
  Transistor #(.width(8)) transistor_4 (.in(del_comp_8_1_var_2_out), .out(transistor_1_out), .gate(compare_8_1_b_2));
  Transistor #(.width(8)) transistor_5 (.in({8{1'b0}}), .out(out_4), .gate(Stop));
  Transistor #(.\type ("n"), .gate("br"), .width(8)) transistor_6 (.in(transistor_1_out), .out(out_4), .gate(Stop));
  Transistor #(.\type ("n"), .width(8)) transistor_7 (.in(transistor_2_out), .out(out_5), .gate(Stop));
  Transistor #(.width(8)) transistor_8 (.in(out_4), .out(out_5), .gate(Stop));
endmodule
