// Logisim project SUM_1.circ as structural Verilog: 1 circuit, main circuit SUM_1
module SUM_1 (
  input  in_1,
  input  in_2,
  input  in_3,
  output out_4,
  output out_5
);

  wire nand_1_out, nand_2_out, nand_3_out, xor_1_out;

  xor xor_1 (xor_1_out, in_1, in_2);
  xor xor_2 (out_4, xor_1_out, in_3);
  nand nand_1 (nand_1_out, in_3, in_2);
  nand nand_2 (nand_2_out, in_1, in_3);
  nand nand_3 (nand_3_out, in_2, in_1);
  nand nand_4 (out_5, nand_1_out, nand_2_out, nand_3_out);
endmodule
