// Logisim project SUM_8v2.circ as structural Verilog: 1 circuit, main circuit SUM_8
module SUM_8 (
  input  [7:0] in_1,
  input  [7:0] in_2,
  output [7:0] out_3,
  output out_4
);

  wire sum_1_1_out_5, sum_1_2_out_5, sum_1_3_out_5, sum_1_4_out_5, sum_1_5_out_5, sum_1_6_out_5,
       sum_1_7_out_5;

  SUM_1 sum_1_1 (.in_1(in_1[0]), .in_2(in_2[0]), .in_3(1'b0), .out_4(out_3[0]), .out_5(sum_1_1_out_5));
  SUM_1 sum_1_2 (.in_1(in_1[1]), .in_2(in_2[1]), .in_3(sum_1_1_out_5), .out_4(out_3[1]), .out_5(sum_1_2_out_5));
  SUM_1 sum_1_3 (.in_1(in_1[2]), .in_2(in_2[2]), .in_3(sum_1_2_out_5), .out_4(out_3[2]), .out_5(sum_1_3_out_5));
  SUM_1 sum_1_4 (.in_1(in_1[3]), .in_2(in_2[3]), .in_3(sum_1_3_out_5), .out_4(out_3[3]), .out_5(sum_1_4_out_5));
  SUM_1 sum_1_5 (.in_1(in_1[4]), .in_2(in_2[4]), .in_3(sum_1_4_out_5), .out_4(out_3[4]), .out_5(sum_1_5_out_5));
  SUM_1 sum_1_6 (.in_1(in_1[5]), .in_2(in_2[5]), .in_3(sum_1_5_out_5), .out_4(out_3[5]), .out_5(sum_1_6_out_5));
  SUM_1 sum_1_7 (.in_1(in_1[6]), .in_2(in_2[6]), .in_3(sum_1_6_out_5), .out_4(out_3[6]), .out_5(sum_1_7_out_5));
  SUM_1 sum_1_8 (.in_1(in_1[7]), .in_2(in_2[7]), .in_3(sum_1_7_out_5), .out_4(out_3[7]), .out_5(out_4));
endmodule
