// Logisim project SUM_8v3.circ as structural Verilog: 1 circuit, main circuit SUM_8
module SUM_8 (
  input  [7:0] in_1,
  input  [7:0] in_2,
  input  start,
  output [7:0] out_4,
  output out_5,
  output stop
);

  wire del_comp_8_1_out, not_1_out, not_2_out, not_3_out, sum_1_1_out_5, sum_1_2_out_5, sum_1_3_out_5,
       sum_1_4_out_5, sum_1_5_out_5, sum_1_6_out_5, sum_1_7_out_5, transistor_1_out;

  SUM_1 sum_1_1 (.in_1(in_1[0]), .in_2(in_2[0]), .in_3(1'b0), .out_4(out_4[0]), .out_5(sum_1_1_out_5));
  SUM_1 sum_1_2 (.in_1(in_1[1]), .in_2(in_2[1]), .in_3(sum_1_1_out_5), .out_4(out_4[1]), .out_5(sum_1_2_out_5));
  SUM_1 sum_1_3 (.in_1(in_1[2]), .in_2(in_2[2]), .in_3(sum_1_2_out_5), .out_4(out_4[2]), .out_5(sum_1_3_out_5));
  SUM_1 sum_1_4 (.in_1(in_1[3]), .in_2(in_2[3]), .in_3(sum_1_3_out_5), .out_4(out_4[3]), .out_5(sum_1_4_out_5));
  SUM_1 sum_1_5 (.in_1(in_1[4]), .in_2(in_2[4]), .in_3(sum_1_4_out_5), .out_4(out_4[4]), .out_5(sum_1_5_out_5));
  SUM_1 sum_1_6 (.in_1(in_1[5]), .in_2(in_2[5]), .in_3(sum_1_5_out_5), .out_4(out_4[5]), .out_5(sum_1_6_out_5));
  SUM_1 sum_1_7 (.in_1(in_1[6]), .in_2(in_2[6]), .in_3(sum_1_6_out_5), .out_4(out_4[6]), .out_5(sum_1_7_out_5));
  SUM_1 sum_1_8 (.in_1(in_1[7]), .in_2(in_2[7]), .in_3(sum_1_7_out_5), .out_4(out_4[7]), .out_5(out_5));
  Transistor #(.\type ("n")) transistor_1 (.in(start), .out(transistor_1_out), .gate(del_comp_8_1_out));
  Del_comp_8 del_comp_8_1 (.var_2_in(out_4), .start(start), .out(del_comp_8_1_out));  // open: var_2_out
  Transistor transistor_2 (.in(1'b0), .out(transistor_1_out), .gate(del_comp_8_1_out));
  not not_1 (not_1_out, not_2_out);
  not not_2 (not_2_out, transistor_1_out);
  not not_3 (not_3_out, not_1_out);
  not not_4 (stop, not_3_out);
endmodule
