// Logisim project Sum_neg.circ as structural Verilog: 1 circuit, main circuit Sum_sub_neg
module Sum_sub_neg (
  input  in_1,
  input  X__minus,
  input  [7:0] Val_X,
  input  Y__minus,
  input  [7:0] Val_Y,
  input  Start,
  output [7:0] val_out,
  output stop,
  output minus
);

  wire and_1_out, and_2_out, and_3_out, and_4_out, ex, or_1_out, or_2_out, stop1, stop2, stop3, stop4,
       sub_sequence_1_stop, sub_sequence_2_stop, X, Y;
  wire [7:0] sub_8_1_out_4, sub_8_2_out_4, sub_sequence_1_out_4, sub_sequence_1_out_5, sub_sequence_2_out_4,
       sub_sequence_2_out_5, sum_8_1_out_4, sum_8_2_out_4, transistor_1_out, transistor_3_out,
       transistor_5_out;

  // XOR_Gate xor_1 has open pins: in0=Y__minus, in1=X__minus, out=open
  SUB_SEQUENCE sub_sequence_1 (
    .in_1(Val_Y), .in_2(Val_X), .start(Start), .out_4(sub_sequence_1_out_4), .out_5(sub_sequence_1_out_5),
    .Stop(sub_sequence_1_stop));
  SUB_SEQUENCE sub_sequence_2 (
    .in_1(Val_Y), .in_2(Val_X), .start(Start), .out_4(sub_sequence_2_out_4), .out_5(sub_sequence_2_out_5),
    .Stop(sub_sequence_2_stop));
  COMPARE_8 compare_8_1 (.A(Val_Y), .B(Val_X), .A_2(X), .B_2(Y));  // open: out_4
  xor xor_2 (ex, Y__minus, X__minus);
  SUM_8 sum_8_1 (.in_1(Val_Y), .in_2(Val_X), .out_4(sum_8_1_out_4), .start(Start), .stop(stop1));  // open: out_5
  SUB_8 sub_8_1 (
    .in_1(sub_sequence_1_out_4), .in_2(sub_sequence_1_out_5), .out_4(sub_8_1_out_4),
    .start(sub_sequence_1_stop), .stop(stop2));  // open: out_5
  SUM_8 sum_8_2 (.in_1(Val_Y), .in_2(Val_X), .out_4(sum_8_2_out_4), .start(Start), .stop(stop3));  // open: out_5
  SUB_8 sub_8_2 (
    .in_1(sub_sequence_2_out_4), .in_2(sub_sequence_2_out_5), .out_4(sub_8_2_out_4),
    .start(sub_sequence_2_stop), .stop(stop4));  // open: out_5
  and and_1 (and_1_out, Y__minus, X);
  and and_2 (and_2_out, Y, X__minus);
  Transistor #(.width(8)) transistor_1 (.in(sum_8_1_out_4), .out(transistor_1_out), .gate(ex));
  Transistor #(.\type ("n"), .width(8)) transistor_2 (.in(sub_8_1_out_4), .out(transistor_1_out), .gate(ex));
  Transistor #(.\type ("n"), .width(8)) transistor_3 (.in(sum_8_2_out_4), .out(transistor_3_out), .gate(ex));
  Transistor #(.width(8)) transistor_4 (.in(sub_8_2_out_4), .out(transistor_3_out), .gate(ex));
  or or_1 (or_1_out, stop2, stop4);
  or or_2 (or_2_out, and_1_out, and_2_out);
  Transistor #(.width(8)) transistor_5 (.in(transistor_1_out), .out(transistor_5_out), .gate(in_1));
  Transistor #(.\type ("n"), .width(8)) transistor_6 (.in(transistor_3_out), .out(transistor_5_out), .gate(in_1));
  and and_3 (and_3_out, in_1, Y);
  and and_4 (and_4_out, Y__minus, ~ex, X__minus);  // AND_Gate
  Del_comp_8 del_comp_8_1 (.var_2_in(transistor_5_out), .start(or_1_out), .var_2_out(val_out), .out(stop));
  or or_3 (minus, and_3_out, or_2_out, and_4_out);

  // Other names for the same wires on the sheet: tunnel = in_1; val_X_t[7:0] = Val_Y; val_Y_t[7:0] = Val_X;
  //   X__minus_t = Y__minus; Y__minus_t = X__minus

  // Notes on the sheet:
  //   dla sumy
  //   dla roznicy
endmodule
