// Logisim project comp_1.circ as structural Verilog: 1 circuit, main circuit COMPARE_1
module COMPARE_1 (
  input  A,
  input  B,
  input  in_3,
  output out_4,
  output out_5,
  output out_6
);

  wire nand_1_out, nand_2_out, nand_3_out, not_1_out, not_2_out;

  not not_1 (not_1_out, B);
  not not_2 (not_2_out, A);
  nand nand_1 (nand_1_out, A, not_1_out, in_3);
  nand nand_2 (nand_2_out, in_3, B, not_2_out);
  not not_3 (out_4, nand_1_out);
  not not_4 (out_6, nand_2_out);
  nand nand_3 (nand_3_out, nand_1_out, in_3, nand_2_out);
  not not_5 (out_5, nand_3_out);
endmodule
