// Logisim project comp_D_8v2.circ as structural Verilog: 1 circuit, main circuit comp_delay_8
module comp_delay_8 (
  input  [7:0] var_2,
  input  start,
  output [7:0] var_2_2,
  output out_4
);

  wire and_1_out, compare_8_1_a_2, compare_8_1_b_2, compare_8_1_out_4, not_1_out, not_2_out,
       transistor_2_out, transistor_3_out, transistor_4_out, transistor_5_out, transistor_6_out,
       transistor_7_out, transistor_8_out, transistor_9_out, transistor_18_out, transistor_19_out,
       transistor_20_out, transistor_21_out, transistor_22_out, transistor_23_out, transistor_24_out,
       transistor_25_out, transistor_34_out, transistor_35_out, transistor_36_out, transistor_37_out,
       transistor_38_out, transistor_39_out, transistor_40_out, transistor_41_out;
  wire [7:0] transistor_1_out, transistor_50_out;

  Transistor #(.\type ("n"), .gate("br"), .width(8)) transistor_1 (.in(var_2), .out(transistor_1_out), .gate(start));
  Transistor #(.\type ("n")) transistor_2 (
    .in(transistor_1_out[0]), .out(transistor_2_out), .gate(transistor_1_out[0]));
  Transistor #(.\type ("n")) transistor_3 (
    .in(transistor_1_out[1]), .out(transistor_3_out), .gate(transistor_1_out[1]));
  Transistor #(.\type ("n")) transistor_4 (
    .in(transistor_1_out[2]), .out(transistor_4_out), .gate(transistor_1_out[2]));
  Transistor #(.\type ("n")) transistor_5 (
    .in(transistor_1_out[3]), .out(transistor_5_out), .gate(transistor_1_out[3]));
  Transistor #(.\type ("n")) transistor_6 (
    .in(transistor_1_out[4]), .out(transistor_6_out), .gate(transistor_1_out[4]));
  Transistor #(.\type ("n")) transistor_7 (
    .in(transistor_1_out[5]), .out(transistor_7_out), .gate(transistor_1_out[5]));
  Transistor #(.\type ("n")) transistor_8 (
    .in(transistor_1_out[6]), .out(transistor_8_out), .gate(transistor_1_out[6]));
  Transistor #(.\type ("n")) transistor_9 (
    .in(transistor_1_out[7]), .out(transistor_9_out), .gate(transistor_1_out[7]));
  Transistor transistor_10 (.in(1'b0), .out(transistor_2_out), .gate(transistor_1_out[0]));
  Transistor transistor_11 (.in(1'b0), .out(transistor_5_out), .gate(transistor_1_out[3]));
  Transistor transistor_12 (.in(1'b0), .out(transistor_3_out), .gate(transistor_1_out[1]));
  Transistor transistor_13 (.in(1'b0), .out(transistor_4_out), .gate(transistor_1_out[2]));
  Transistor transistor_14 (.in(1'b0), .out(transistor_7_out), .gate(transistor_1_out[5]));
  Transistor transistor_15 (.in(1'b0), .out(transistor_8_out), .gate(transistor_1_out[6]));
  Transistor transistor_16 (.in(1'b0), .out(transistor_6_out), .gate(transistor_1_out[4]));
  Transistor transistor_17 (.in(1'b0), .out(transistor_9_out), .gate(transistor_1_out[7]));
  Transistor #(.\type ("n")) transistor_18 (.in(transistor_2_out), .out(transistor_18_out), .gate(transistor_2_out));
  Transistor #(.\type ("n")) transistor_19 (.in(transistor_3_out), .out(transistor_19_out), .gate(transistor_3_out));
  Transistor #(.\type ("n")) transistor_20 (.in(transistor_4_out), .out(transistor_20_out), .gate(transistor_4_out));
  Transistor #(.\type ("n")) transistor_21 (.in(transistor_5_out), .out(transistor_21_out), .gate(transistor_5_out));
  Transistor #(.\type ("n")) transistor_22 (.in(transistor_6_out), .out(transistor_22_out), .gate(transistor_6_out));
  Transistor #(.\type ("n")) transistor_23 (.in(transistor_7_out), .out(transistor_23_out), .gate(transistor_7_out));
  Transistor #(.\type ("n")) transistor_24 (.in(transistor_8_out), .out(transistor_24_out), .gate(transistor_8_out));
  Transistor #(.\type ("n")) transistor_25 (.in(transistor_9_out), .out(transistor_25_out), .gate(transistor_9_out));
  Transistor transistor_26 (.in(1'b0), .out(transistor_18_out), .gate(transistor_2_out));
  Transistor transistor_27 (.in(1'b0), .out(transistor_20_out), .gate(transistor_4_out));
  Transistor transistor_28 (.in(1'b0), .out(transistor_21_out), .gate(transistor_5_out));
  Transistor transistor_29 (.in(1'b0), .out(transistor_19_out), .gate(transistor_3_out));
  Transistor transistor_30 (.in(1'b0), .out(transistor_23_out), .gate(transistor_7_out));
  Transistor transistor_31 (.in(1'b0), .out(transistor_22_out), .gate(transistor_6_out));
  Transistor transistor_32 (.in(1'b0), .out(transistor_24_out), .gate(transistor_8_out));
  Transistor transistor_33 (.in(1'b0), .out(transistor_25_out), .gate(transistor_9_out));
  Transistor #(.\type ("n")) transistor_34 (.in(transistor_18_out), .out(transistor_34_out), .gate(transistor_18_out));
  Transistor #(.\type ("n")) transistor_35 (.in(transistor_19_out), .out(transistor_35_out), .gate(transistor_19_out));
  Transistor #(.\type ("n")) transistor_36 (.in(transistor_20_out), .out(transistor_36_out), .gate(transistor_20_out));
  Transistor #(.\type ("n")) transistor_37 (.in(transistor_21_out), .out(transistor_37_out), .gate(transistor_21_out));
  Transistor #(.\type ("n")) transistor_38 (.in(transistor_22_out), .out(transistor_38_out), .gate(transistor_22_out));
  Transistor #(.\type ("n")) transistor_39 (.in(transistor_23_out), .out(transistor_39_out), .gate(transistor_23_out));
  Transistor #(.\type ("n")) transistor_40 (.in(transistor_24_out), .out(transistor_40_out), .gate(transistor_24_out));
  Transistor #(.\type ("n")) transistor_41 (.in(transistor_25_out), .out(transistor_41_out), .gate(transistor_25_out));
  Transistor transistor_42 (.in(1'b0), .out(transistor_34_out), .gate(transistor_18_out));
  Transistor transistor_43 (.in(1'b0), .out(transistor_36_out), .gate(transistor_20_out));
  Transistor transistor_44 (.in(1'b0), .out(transistor_35_out), .gate(transistor_19_out));
  Transistor transistor_45 (.in(1'b0), .out(transistor_38_out), .gate(transistor_22_out));
  Transistor transistor_46 (.in(1'b0), .out(transistor_39_out), .gate(transistor_23_out));
  Transistor transistor_47 (.in(1'b0), .out(transistor_37_out), .gate(transistor_21_out));
  Transistor transistor_48 (.in(1'b0), .out(transistor_41_out), .gate(transistor_25_out));
  Transistor transistor_49 (.in(1'b0), .out(transistor_40_out), .gate(transistor_24_out));
  Transistor #(.\type ("n")) transistor_50 (
    .in(transistor_34_out), .out(transistor_50_out[0]), .gate(transistor_34_out));
  Transistor #(.\type ("n")) transistor_51 (
    .in(transistor_35_out), .out(transistor_50_out[1]), .gate(transistor_35_out));
  Transistor #(.\type ("n")) transistor_52 (
    .in(transistor_36_out), .out(transistor_50_out[2]), .gate(transistor_36_out));
  Transistor #(.\type ("n")) transistor_53 (
    .in(transistor_37_out), .out(transistor_50_out[3]), .gate(transistor_37_out));
  Transistor #(.\type ("n")) transistor_54 (
    .in(transistor_38_out), .out(transistor_50_out[4]), .gate(transistor_38_out));
  Transistor #(.\type ("n")) transistor_55 (
    .in(transistor_39_out), .out(transistor_50_out[5]), .gate(transistor_39_out));
  Transistor #(.\type ("n")) transistor_56 (
    .in(transistor_40_out), .out(transistor_50_out[6]), .gate(transistor_40_out));
  Transistor #(.\type ("n")) transistor_57 (
    .in(transistor_41_out), .out(transistor_50_out[7]), .gate(transistor_41_out));
  Transistor transistor_58 (.in(1'b0), .out(transistor_50_out[0]), .gate(transistor_34_out));
  Transistor transistor_59 (.in(1'b0), .out(transistor_50_out[1]), .gate(transistor_35_out));
  Transistor transistor_60 (.in(1'b0), .out(transistor_50_out[2]), .gate(transistor_36_out));
  Transistor transistor_61 (.in(1'b0), .out(transistor_50_out[5]), .gate(transistor_39_out));
  Transistor transistor_62 (.in(1'b0), .out(transistor_50_out[3]), .gate(transistor_37_out));
  Transistor transistor_63 (.in(1'b0), .out(transistor_50_out[4]), .gate(transistor_38_out));
  Transistor transistor_64 (.in(1'b0), .out(transistor_50_out[6]), .gate(transistor_40_out));
  Transistor transistor_65 (.in(1'b0), .out(transistor_50_out[7]), .gate(transistor_41_out));
  COMPARE_8 compare_8_1 (
    .A(var_2), .B(transistor_50_out), .A_2(compare_8_1_a_2), .out_4(compare_8_1_out_4), .B_2(compare_8_1_b_2));
  not not_1 (not_1_out, compare_8_1_a_2);
  and and_1 (and_1_out, not_1_out, compare_8_1_out_4, not_2_out);
  not not_2 (not_2_out, compare_8_1_b_2);
  Transistor #(.\type ("n"), .gate("br")) transistor_66 (.in(and_1_out), .out(out_4), .gate(start));
  Transistor #(.gate("br")) transistor_67 (.in(1'b0), .out(out_4), .gate(start));

  assign var_2_2 = var_2;
endmodule
